// Logisim project cpu21-riscv.circ as structural Verilog: 17 circuits, main circuit ◇单周期RISC-V
module \单周期RISC_V  (
  input  IR1,
  input  IR2,
  input  IR3,
  output RegWrite,
  output MemWrite,
  output [31:0] PC,
  output [31:0] IR,
  output [31:0] RDin,
  output [31:0] MDin,
  output [31:0] LedData
);

  wire alu_1_equal, alu_1_out_6, and_1_out, and_2_out, and_3_out, and_4_out, Bltu, Byte, CLK, clock_2_out,
       comparator_1_eq, comparator_2_eq, comparator_3_eq, comparator_3_lt, controlled_buffer_1_out, d_ff_1_q,
       ecall, Go, halt, IR1_t, IR2_t, IR3_t, IRA, IRB, IRC, jal, jalr, jmp, MemToReg, nand_1_out, not_1_out,
       not_2_out, not_3_out, not_4_out, or_4_out, RST, Run, S_type, W1, W2, W3, \单周期硬布线控制器_1_alu_src ,
       \单周期硬布线控制器_1_beq , \单周期硬布线控制器_1_bne ;
  wire [0:0] adder_6_out_2;
  wire [1:0] adder_1_out, adder_2_out, bit_extender_1_out, multiplexer_2_out, multiplexer_3_out;
  wire [3:0] AluOP;
  wire [4:0] multiplexer_4_out, multiplexer_5_out;
  wire [7:0] multiplexer_9_out;
  wire [12:0] CNT_num;
  wire [15:0] \总周期数 ;
  wire [31:0] adder_4_out, adder_5_out, bit_extender_2_out, bit_extender_3_out, bit_extender_4_out,
       bit_extender_5_out, bit_extender_6_out, multiplexer_1_out, multiplexer_6_out, multiplexer_7_out,
       multiplexer_8_out, PC_4, R1, ram_1_data, Result, Result2, shifter_1_out, shifter_2_out;
  wire [31:1] adder_6_out;

  Clock #(.highDuration(1), .lowDuration(1)) clock_1 (.out(CLK));
  Button _1 (.out(IRA));
  Button _2 (.out(IRB));
  Button _3 (.out(IRC));
  Button \u_继续运行  (.out(Go));
  LED #(.active("true")) led_1 (.in(W1));
  LED #(.active("true")) led_2 (.in(W2));
  LED #(.active("true")) led_3 (.in(W3));
  assign bit_extender_1_out = {{1{1'b0}}, or_4_out};  // Bit_Extender bit_extender_1
  not not_1 (not_1_out, halt);
  Multiplexer #(.select(2), .width(32), .disabled("Z"), .enable("false")) multiplexer_1 (
    .in0(PC_4), .in1(adder_4_out), .in2(adder_5_out), .in3({adder_6_out, 1'b0}), .out(multiplexer_1_out),
    .sel(adder_2_out));
  Hex_Digit_Display hex_digit_display_1 (.value(LedData[31:28]));  // open: dp
  Adder #(.width(2)) adder_1 (.a(bit_extender_1_out), .b(multiplexer_2_out), .out(adder_1_out));  // open: cin, cout
  or or_1 (Run, Go, not_1_out);
  Register #(.width(32), .trigger("rising"), .Select("low")) u_PC (
    .D(multiplexer_1_out), .en(Run), .Q(PC), .clk(CLK));  // open: clr
  Hex_Digit_Display hex_digit_display_2 (.value(LedData[23:20]));  // open: dp
  Hex_Digit_Display hex_digit_display_3 (.value(LedData[27:24]));  // open: dp
  Adder #(.width(2)) adder_2 (.a(adder_1_out), .b(multiplexer_3_out), .out(adder_2_out));  // open: cin, cout
  Hex_Digit_Display hex_digit_display_4 (.value(LedData[19:16]));  // open: dp
  Hex_Digit_Display hex_digit_display_5 (.value(LedData[15:12]));  // open: dp
  // RiscV_Probe riscv_probe_1: pin names not known; wires that end beside it: RST, IR
  Adder #(.width(32)) adder_3 (.a(PC), .b(32'h4), .out(PC_4));  // open: cin, cout
  Hex_Digit_Display hex_digit_display_6 (.value(LedData[7:4]));  // open: dp
  Hex_Digit_Display hex_digit_display_7 (.value(LedData[11:8]));  // open: dp
  // Probe on \总周期数 
  Multiplexer #(.select(1), .width(2), .disabled("Z"), .enable("false")) multiplexer_2 (
    .in0(2'b00), .in1(2'b10), .out(multiplexer_2_out), .sel(jal));
  Multiplexer #(.select(1), .width(2), .disabled("Z"), .enable("false")) multiplexer_3 (
    .in0(2'b00), .in1(2'b11), .out(multiplexer_3_out), .sel(jalr));
  ROM #(.addrWidth(10), .dataWidth(32), .Select("high")) rom_1 (.addr(PC[11:2]), .data(IR));
  Hex_Digit_Display hex_digit_display_8 (.value(LedData[3:0]));  // open: dp
  \单周期硬布线控制器  \u_单周期硬布线控制器_1  (
    .Funct({IR[30], IR[25], IR[14:12]}), .OP(IR[6:2]), .ALU_OP(AluOP), .MemToReg(MemToReg),
    .MemWrite(MemWrite), .ALU_SRC(\单周期硬布线控制器_1_alu_src ), .RegWrite(RegWrite), .ecall(ecall),
    .S_type(S_type), .Jalr(jalr), .Beq(\单周期硬布线控制器_1_beq ), .JAL(jal), .Bne(\单周期硬布线控制器_1_bne ), .Bltu(Bltu),
    .Byte(Byte));
  or or_2 (IR1_t, IR1, IRA);
  Multiplexer #(.select(1), .width(5), .disabled("Z"), .enable("false")) multiplexer_4 (
    .in0(IR[19:15]), .in1(5'b10001), .out(multiplexer_4_out), .sel(ecall));
  Multiplexer #(.select(1), .width(5), .disabled("Z"), .enable("false")) multiplexer_5 (
    .in0(IR[24:20]), .in1(5'b01010), .out(multiplexer_5_out), .sel(ecall));
  assign bit_extender_2_out = {{20{IR[31]}}, {IR[31], IR[7], IR[30:25], IR[11:8]}};  // Bit_Extender bit_extender_2
  assign bit_extender_3_out = {{12{IR[31]}}, {IR[31], IR[19:12], IR[20], IR[30:21]}};  // Bit_Extender bit_extender_3
  or or_3 (IR2_t, IR2, IRB);
  or or_4 (or_4_out, and_3_out, and_2_out, and_1_out);
  Regifile regifile_1 (
    .Din(RDin), .Clk(CLK), .R1(R1), .R2(MDin), .WE(RegWrite), .W_num(IR[11:7]), .R1_num(multiplexer_4_out),
    .R2_num(multiplexer_5_out));
  assign bit_extender_4_out = {{20{IR[31]}}, IR[31:20]};  // Bit_Extender bit_extender_4
  assign bit_extender_5_out = {{20{IR[31]}}, {IR[31:25], IR[11:7]}};  // Bit_Extender bit_extender_5
  Shifter #(.width(32), .shift("ll")) shifter_1 (.in(bit_extender_2_out), .\dist (5'b00001), .out(shifter_1_out));
  Shifter #(.width(32), .shift("ll")) shifter_2 (.in(bit_extender_3_out), .\dist (5'b00001), .out(shifter_2_out));
  Multiplexer #(.select(1), .width(32), .disabled("Z"), .enable("false")) multiplexer_6 (
    .in0(MDin), .in1(multiplexer_7_out), .out(multiplexer_6_out), .sel(\单周期硬布线控制器_1_alu_src ));
  Multiplexer #(.select(1), .width(32), .disabled("Z"), .enable("false")) multiplexer_7 (
    .in0(bit_extender_4_out), .in1(bit_extender_5_out), .out(multiplexer_7_out), .sel(S_type));
  Adder #(.width(32)) adder_4 (.a(shifter_1_out), .b(PC), .out(adder_4_out));  // open: cin, cout
  Adder #(.width(32)) adder_5 (.a(shifter_2_out), .b(PC), .out(adder_5_out));  // open: cin, cout
  or or_5 (IR3_t, IR3, IRC);
  and and_1 (and_1_out, \单周期硬布线控制器_1_bne , not_2_out);
  and and_2 (and_2_out, \单周期硬布线控制器_1_beq , alu_1_equal);
  not not_2 (not_2_out, alu_1_equal);
  Adder #(.width(32)) adder_6 (
    .a(R1), .b(multiplexer_7_out), .out({adder_6_out, adder_6_out_2[0]}));  // open: cin, cout
  and and_3 (and_3_out, Bltu, alu_1_out_6);
  ALU alu_1 (
    .X(R1), .Y(multiplexer_6_out), .AluOP(AluOP), .Equal(alu_1_equal), .Result(Result), .Result_2(Result2),
    .out_6(alu_1_out_6));  // open: out_4
  or or_6 (jmp, jal, jalr);
  Comparator #(.width(32), .mode("twosComplement")) comparator_1 (
    .a(R1), .b(32'h32), .eq(comparator_1_eq));  // open: gt, lt
  and and_4 (and_4_out, ecall, not_3_out);
  not not_3 (not_3_out, comparator_1_eq);
  and and_5 (halt, ecall, comparator_1_eq);
  Comparator #(.width(4), .mode("twosComplement")) comparator_2 (
    .a(AluOP), .b(4'b1101), .eq(comparator_2_eq));  // open: gt, lt
  Multiplexer #(.select(1), .width(32), .disabled("Z"), .enable("false")) multiplexer_8 (
    .in0(Result), .in1(Result2), .out(multiplexer_8_out), .sel(comparator_2_eq));
  RAM #(.addrWidth(10), .dataWidth(32), .bus("separate"), .Select("high")) ram_1 (
    .addr(Result[11:2]), .din(MDin), .data(ram_1_data), .str(MemWrite), .clk(CLK), .ld(MemToReg));  // open: sel, clr
  Register #(.width(32), .trigger("rising"), .Select("low")) register_1 (
    .D(MDin), .en(and_4_out), .Q(LedData), .clk(CLK));  // open: clr
  Multiplexer #(.select(2), .width(8), .disabled("Z"), .enable("false")) multiplexer_9 (
    .in0(ram_1_data[7:0]), .in1(ram_1_data[15:8]), .in2(ram_1_data[23:16]), .in3(ram_1_data[31:24]),
    .out(multiplexer_9_out), .sel(Result[1:0]));
  D_Flip_Flop #(.trigger("high"), .Pre_Clr_Positions("LEGACY"), .NegatePresetClear("false"), .enable("true"), .NewFFLayout("false")) d_ff_1 (.Q(d_ff_1_q));  // open: clk, D, Qn, preset, en, reset
  // Probe on 13'hc
  Multiplexer #(.select(3), .width(32), .disabled("Z"), .enable("false")) multiplexer_10 (
    .in0(multiplexer_8_out), .in1(ram_1_data), .in2(PC_4), .in5(bit_extender_6_out), .out(RDin),
    .sel({Byte, jmp, MemToReg}));  // open: in3, in4, in6, in7
  assign bit_extender_6_out = {{24{1'b0}}, multiplexer_9_out};  // Bit_Extender bit_extender_6
  Comparator #(.width(13), .mode("twosComplement")) comparator_3 (
    .a(CNT_num), .b(13'hc), .eq(comparator_3_eq), .lt(comparator_3_lt));  // open: gt
  Clock #(.highDuration(1), .lowDuration(1)) clock_2 (.out(clock_2_out));
  not not_4 (not_4_out, halt);
  Counter #(.width(16), .max('hffff), .ongoal("wrap"), .trigger("rising"), .behavior("new")) counter_1 (
    .count(not_4_out), .Q(\总周期数 ), .clk(CLK));  // open: load, D, carry, clr, preset, down
  Counter #(.width(13), .max('h1fff), .ongoal("stay"), .trigger("rising"), .behavior("old")) counter_2 (
    .count(comparator_3_lt), .Q(CNT_num), .clk(clock_2_out));  // open: load, D, carry, clr, preset
  nand nand_1 (nand_1_out, d_ff_1_q, comparator_3_eq);
  assign controlled_buffer_1_out = nand_1_out ? clock_2_out : 1'bz;  // Controlled_Buffer controlled_buffer_1
  Pull_Resistor #(.pull(1)) pull_resistor_1 (.node(controlled_buffer_1_out));

  // Other names for the same wires on the sheet: R2[31:0] = MDin

  // Notes on the sheet:
  //   中断源
  //   中断等待指示
  //   总复位信号应将除ROM以外所有存储组件全部清零
  //   三种分支不同时出现，用加法整合
  //   数码管输出
  //   指令存储器
  //   数码管输出应该用寄存器锁存，否则显示数据只能一闪而过
  //   指令字
  //   contents of rom_1 (hex, n*v repeats v):
  //   100493 100006f 100493 200913 300993 100006f 100493 200913 300993 100006f 100493 200913 300993
  //   100006f 100493 200913 300993 3c4000ef 100413 100493 1f49493 900533 2200893 73 24d493 48463 fedff06f
  //   900533 2200893 73 100493 249493 900533 2200893 73 48463 fedff06f 100493 1f49493 900533 2200893 73
  //   4034d493 900533 2200893 73 4044d493 900533 2200893 73 4044d493 900533 2200893 73 4044d493 900533
  //   2200893 73 4044d493 900533 2200893 73 4044d493 900533 2200893 73 4044d493 900533 2200893 73 4044d493
  //   900533 2200893 73 100413 1f41993 41f9d993 433 c00913 300b13 140413 f47413 800293 100313 499993
  //   89e9b3 1300533 2200893 73 406282b3 fe0294e3 140413 f00f93 1f47433 1c41413 800293 100313 49d993
  //   89e9b3 1300533 2200893 73 406282b3 fe0294e3 1c45413 406b0b33 b0463 f95ff06f 2b3 fff2c293 829293
  //   ff2e293 500533 2200893 73 fff00413 493 84a023 140413 448493 84a023 140413 448493 84a023 140413
  //   448493 84a023 140413 448493 84a023 140413 448493 84a023 140413 448493 84a023 140413 448493 84a023
  //   140413 448493 84a023 140413 448493 84a023 140413 448493 84a023 140413 448493 84a023 140413 448493
  //   84a023 140413 448493 84a023 140413 448493 84a023 140413 448493 84a023 140413 448493 140413 433
  //   3c00493 42983 4aa03 149a2b3 28663 134a023 1442023 ffc48493 fe9412e3 800533 2200893 73 440413 3c00493
  //   fc9416e3 3200893 73 200293 1100493 849493 1148493 1049493 900533 2200893 73 1c00e13 254d4b3 900533
  //   2200893 73 fffe0e13 fe0e16e3 3200893 73 8800493 849493 4848493 8700913 891913 5490913 2997933
  //   1091913 11096913 1200533 2200893 73 3200893 73 313 1000e13 8400493 849493 8348493 400913 891913
  //   490913 849493 8248493 849493 8148493 891913 490913 891913 490913 932023 12484b3 430313 fffe0e13
  //   fe0e18e3 2000e13 313 34483 900533 2200893 73 130313 fffe0e13 fe0e14e3 3200893 73 ff100493 900533
  //   2200893 73 148493 fe9068e3 900533 2200893 73 3200893 73 413 140413 800533 2200893 73 240413 800533
  //   2200893 73 340413 800533 2200893 73 440413 800533 2200893 73 540413 800533 2200893 73 640413 800533
  //   2200893 73 740413 800533 2200893 73 840413 800533 2200893 2200893 73 8067
  //   Beq
  //   Bne
  //   MemToReg
  //   MemWrite
  //   AluOP
  //   AluSrcB
  //   RegWrite
  //   beq/bne的目的地址
  //   jal的目的地址
  //   jalr指令的目的地址
  //   为方便自动评测，需要输出PC，IR，寄存器堆写如数据RDin
  //   数据存储器
  //   RAM写使能MemWrite、RAM写入数据MDin等信号
  //   控制位
  //   暂停节拍，不能为0
  //   戳工具置1进入计数暂停模式，ctrl+k时钟自动运行到对应节拍暂停
  //   ctrl+k关闭时钟连续运行，将控制位置零，进入单步调试模式调试
  //   用这个时钟源需要去掉电路中的其他时钟源
  //   可计数暂停的时钟源
endmodule

// 单周期硬布线控制器
module \单周期硬布线控制器  (
  input  [4:0] OP,
  input  [4:0] Funct,
  output [3:0] ALU_OP,
  output MemToReg,
  output MemWrite,
  output ALU_SRC,
  output RegWrite,
  output ecall,
  output S_type,
  output Beq,
  output Bne,
  output Jalr,
  output JAL,
  output Bltu,
  output Byte
);

  \运算控制器自动生成  \u_运算控制器自动生成_1  (
    .OP2(OP[0]), .OP3(OP[1]), .OP4(OP[2]), .OP5(OP[3]), .OP6(OP[4]), .F12(Funct[0]), .F13(Funct[1]),
    .F14(Funct[2]), .F25(Funct[3]), .F30(Funct[4]), .S0(ALU_OP[0]), .S1(ALU_OP[1]), .S2(ALU_OP[2]),
    .S3(ALU_OP[3]));
  \控制信号自动生成  \u_控制信号自动生成_1  (
    .OP2(OP[0]), .OP3(OP[1]), .OP4(OP[2]), .OP5(OP[3]), .MemToReg(MemToReg), .OP6(OP[4]), .F12(Funct[0]),
    .F13(Funct[1]), .F14(Funct[2]), .F25(Funct[3]), .F30(Funct[4]), .MemWrite(MemWrite), .ALU_SRC(ALU_SRC),
    .RegWrite(RegWrite), .ecall(ecall), .S_Type(S_type), .BEQ(Beq), .BNE(Bne), .JALR(Jalr), .JAL(JAL),
    .BLTU(Bltu), .Byte(Byte));

  // Other names for the same wires on the sheet: OP_CODE[4:0] = OP

  // Notes on the sheet:
  //   运算器控制器，根据指令生成运算器功能选择信号
  //   控制信号生成，产生数据通路需要的其他控制信号
endmodule

// 运算器控制器
module \运算控制器自动生成  (
  input  OP2,
  input  OP3,
  input  OP4,
  input  OP5,
  input  OP6,
  input  F12,
  input  F13,
  input  F14,
  input  F25,
  input  F30,
  output S0,
  output S1,
  output S2,
  output S3
);

  wire and_1_out, and_2_out, and_3_out, and_4_out, and_5_out, and_6_out, and_7_out, and_8_out, and_9_out,
       and_10_out, and_11_out, and_12_out, and_13_out, and_14_out, and_15_out, and_16_out, and_17_out,
       and_18_out, and_19_out, and_20_out, and_21_out, and_22_out, and_23_out, and_24_out, and_25_out,
       and_26_out, and_27_out, and_28_out, and_29_out, and_30_out, and_31_out, and_32_out, not_1_out,
       not_2_out, not_3_out, not_4_out, not_5_out, not_6_out, not_7_out, not_8_out, not_9_out, not_10_out,
       not_11_out, not_12_out, not_13_out, not_14_out, not_15_out, not_16_out, not_17_out, not_18_out,
       not_19_out, not_20_out, not_21_out, not_22_out, not_23_out, not_24_out, not_25_out, not_26_out,
       not_27_out, not_28_out, not_29_out, not_30_out, not_31_out, not_32_out, not_33_out, not_34_out,
       not_35_out, not_36_out, not_37_out, not_38_out, not_39_out, not_40_out, not_41_out, not_42_out,
       not_43_out, not_44_out, not_45_out, not_46_out, not_47_out, not_48_out, not_49_out, not_50_out,
       not_51_out, not_52_out, not_53_out, not_54_out, not_55_out, not_56_out, not_57_out, not_58_out,
       not_59_out, not_60_out, not_61_out, not_62_out, not_63_out, not_64_out, not_65_out, not_66_out,
       not_67_out, not_68_out, not_69_out, not_70_out, not_71_out, not_72_out, not_73_out, not_74_out,
       not_75_out, not_76_out, not_77_out, not_78_out, not_79_out, not_80_out, not_81_out, not_82_out,
       not_83_out, not_84_out, not_85_out, not_86_out, not_87_out, not_88_out, not_89_out, not_90_out,
       not_91_out, not_92_out, not_93_out, not_94_out, not_95_out, not_96_out, not_97_out, not_98_out,
       not_99_out, not_100_out, not_101_out, not_102_out, not_103_out, not_104_out, not_105_out, not_106_out,
       not_107_out, not_108_out, not_109_out, not_110_out, not_111_out, not_112_out, not_113_out,
       not_114_out, not_115_out, not_116_out, not_117_out, not_118_out, not_119_out, not_120_out,
       not_121_out, not_122_out, not_123_out, not_124_out, not_125_out, not_126_out, not_127_out,
       not_128_out, not_129_out, not_130_out, not_131_out, not_132_out, not_133_out, not_134_out,
       not_135_out, not_136_out, not_137_out, not_138_out, not_139_out, not_140_out, not_141_out,
       not_142_out, not_143_out, not_144_out, not_145_out, not_146_out, not_147_out, not_148_out,
       not_149_out, not_150_out, not_151_out, not_152_out, not_153_out, not_154_out, not_155_out,
       not_156_out, not_157_out, not_158_out, not_159_out, not_160_out, not_161_out, not_162_out,
       not_163_out, not_164_out, not_165_out, not_166_out, not_167_out, not_168_out, not_169_out,
       not_170_out, not_171_out, not_172_out, not_173_out, not_174_out, not_175_out, not_176_out,
       not_177_out, not_178_out, not_179_out, not_180_out, not_181_out, not_182_out, not_183_out,
       not_184_out, not_185_out, not_186_out;

  not not_1 (not_1_out, F30);
  not not_2 (not_2_out, F25);
  not not_3 (not_3_out, F14);
  not not_4 (not_4_out, F13);
  not not_5 (not_5_out, F12);
  not not_6 (not_6_out, OP6);
  not not_7 (not_7_out, OP3);
  not not_8 (not_8_out, OP2);
  not not_9 (not_9_out, F30);
  not not_10 (not_10_out, F25);
  not not_11 (not_11_out, OP6);
  not not_12 (not_12_out, OP3);
  not not_13 (not_13_out, OP2);
  not not_14 (not_14_out, F30);
  not not_15 (not_15_out, F25);
  not not_16 (not_16_out, F14);
  not not_17 (not_17_out, F12);
  not not_18 (not_18_out, OP6);
  not not_19 (not_19_out, OP3);
  not not_20 (not_20_out, OP2);
  not not_21 (not_21_out, F14);
  not not_22 (not_22_out, F13);
  not not_23 (not_23_out, F12);
  not not_24 (not_24_out, OP6);
  not not_25 (not_25_out, OP5);
  not not_26 (not_26_out, OP3);
  not not_27 (not_27_out, OP2);
  not not_28 (not_28_out, OP6);
  not not_29 (not_29_out, OP5);
  not not_30 (not_30_out, OP3);
  not not_31 (not_31_out, OP2);
  not not_32 (not_32_out, F13);
  not not_33 (not_33_out, F12);
  not not_34 (not_34_out, OP6);
  not not_35 (not_35_out, OP5);
  not not_36 (not_36_out, OP3);
  not not_37 (not_37_out, OP2);
  not not_38 (not_38_out, F14);
  not not_39 (not_39_out, F12);
  not not_40 (not_40_out, OP6);
  not not_41 (not_41_out, OP5);
  not not_42 (not_42_out, OP3);
  not not_43 (not_43_out, OP2);
  not not_44 (not_44_out, F25);
  not not_45 (not_45_out, F13);
  not not_46 (not_46_out, OP6);
  not not_47 (not_47_out, OP5);
  not not_48 (not_48_out, OP3);
  not not_49 (not_49_out, OP2);
  not not_50 (not_50_out, F30);
  not not_51 (not_51_out, F12);
  not not_52 (not_52_out, OP6);
  not not_53 (not_53_out, OP3);
  not not_54 (not_54_out, OP2);
  not not_55 (not_55_out, F25);
  not not_56 (not_56_out, F14);
  not not_57 (not_57_out, F13);
  not not_58 (not_58_out, F12);
  not not_59 (not_59_out, OP6);
  not not_60 (not_60_out, OP3);
  not not_61 (not_61_out, OP2);
  not not_62 (not_62_out, F30);
  not not_63 (not_63_out, F25);
  not not_64 (not_64_out, OP6);
  not not_65 (not_65_out, OP3);
  not not_66 (not_66_out, OP2);
  not not_67 (not_67_out, F30);
  not not_68 (not_68_out, F25);
  not not_69 (not_69_out, F14);
  not not_70 (not_70_out, F12);
  not not_71 (not_71_out, OP6);
  not not_72 (not_72_out, OP3);
  not not_73 (not_73_out, OP2);
  not not_74 (not_74_out, OP6);
  not not_75 (not_75_out, OP5);
  not not_76 (not_76_out, OP3);
  not not_77 (not_77_out, OP2);
  not not_78 (not_78_out, F14);
  not not_79 (not_79_out, F12);
  not not_80 (not_80_out, OP6);
  not not_81 (not_81_out, OP5);
  not not_82 (not_82_out, OP3);
  not not_83 (not_83_out, OP2);
  not not_84 (not_84_out, F30);
  not not_85 (not_85_out, F25);
  not not_86 (not_86_out, F13);
  not not_87 (not_87_out, OP6);
  not not_88 (not_88_out, OP5);
  not not_89 (not_89_out, OP3);
  not not_90 (not_90_out, OP2);
  not not_91 (not_91_out, F30);
  not not_92 (not_92_out, F25);
  not not_93 (not_93_out, F14);
  not not_94 (not_94_out, F13);
  not not_95 (not_95_out, F12);
  not not_96 (not_96_out, OP6);
  not not_97 (not_97_out, OP3);
  not not_98 (not_98_out, OP2);
  not not_99 (not_99_out, F25);
  not not_100 (not_100_out, F14);
  not not_101 (not_101_out, F13);
  not not_102 (not_102_out, F12);
  not not_103 (not_103_out, OP6);
  not not_104 (not_104_out, OP3);
  not not_105 (not_105_out, OP2);
  not not_106 (not_106_out, F30);
  not not_107 (not_107_out, F25);
  not not_108 (not_108_out, OP6);
  not not_109 (not_109_out, OP3);
  not not_110 (not_110_out, OP2);
  not not_111 (not_111_out, F30);
  not not_112 (not_112_out, F25);
  not not_113 (not_113_out, F14);
  not not_114 (not_114_out, OP6);
  not not_115 (not_115_out, OP3);
  not not_116 (not_116_out, OP2);
  not not_117 (not_117_out, F14);
  not not_118 (not_118_out, F13);
  not not_119 (not_119_out, F12);
  not not_120 (not_120_out, OP6);
  not not_121 (not_121_out, OP5);
  not not_122 (not_122_out, OP3);
  not not_123 (not_123_out, OP2);
  not not_124 (not_124_out, OP6);
  not not_125 (not_125_out, OP5);
  not not_126 (not_126_out, OP3);
  not not_127 (not_127_out, OP2);
  not not_128 (not_128_out, F30);
  not not_129 (not_129_out, F13);
  not not_130 (not_130_out, OP6);
  not not_131 (not_131_out, OP3);
  not not_132 (not_132_out, OP2);
  not not_133 (not_133_out, F30);
  not not_134 (not_134_out, F12);
  not not_135 (not_135_out, OP6);
  not not_136 (not_136_out, OP3);
  not not_137 (not_137_out, OP2);
  not not_138 (not_138_out, F12);
  not not_139 (not_139_out, OP4);
  not not_140 (not_140_out, OP3);
  not not_141 (not_141_out, OP2);
  not not_142 (not_142_out, F30);
  not not_143 (not_143_out, F25);
  not not_144 (not_144_out, F12);
  not not_145 (not_145_out, OP6);
  not not_146 (not_146_out, OP3);
  not not_147 (not_147_out, OP2);
  not not_148 (not_148_out, F30);
  not not_149 (not_149_out, F25);
  not not_150 (not_150_out, F14);
  not not_151 (not_151_out, F12);
  not not_152 (not_152_out, OP6);
  not not_153 (not_153_out, OP3);
  not not_154 (not_154_out, OP2);
  not not_155 (not_155_out, F30);
  not not_156 (not_156_out, F25);
  not not_157 (not_157_out, F14);
  not not_158 (not_158_out, OP6);
  not not_159 (not_159_out, OP3);
  not not_160 (not_160_out, OP2);
  not not_161 (not_161_out, F12);
  not not_162 (not_162_out, OP6);
  not not_163 (not_163_out, OP5);
  not not_164 (not_164_out, OP3);
  not not_165 (not_165_out, OP2);
  not not_166 (not_166_out, F13);
  not not_167 (not_167_out, F12);
  not not_168 (not_168_out, OP6);
  not not_169 (not_169_out, OP5);
  not not_170 (not_170_out, OP3);
  not not_171 (not_171_out, OP2);
  not not_172 (not_172_out, F14);
  not not_173 (not_173_out, F12);
  not not_174 (not_174_out, OP6);
  not not_175 (not_175_out, OP5);
  not not_176 (not_176_out, OP3);
  not not_177 (not_177_out, OP2);
  not not_178 (not_178_out, F30);
  not not_179 (not_179_out, F12);
  not not_180 (not_180_out, OP6);
  not not_181 (not_181_out, OP3);
  not not_182 (not_182_out, OP2);
  not not_183 (not_183_out, F12);
  not not_184 (not_184_out, OP4);
  not not_185 (not_185_out, OP3);
  not not_186 (not_186_out, OP2);
  and and_1 (and_1_out, not_1_out, not_2_out, not_3_out, not_4_out, not_5_out, not_6_out, OP5, OP4, not_7_out, not_8_out);
  and and_2 (and_2_out, not_9_out, not_10_out, F14, F13, F12, not_11_out, OP5, OP4, not_12_out, not_13_out);
  and and_3 (and_3_out, not_14_out, not_15_out, not_16_out, F13, not_17_out, not_18_out, OP5, OP4, not_19_out, not_20_out);
  and and_4 (and_4_out, not_21_out, not_22_out, not_23_out, not_24_out, not_25_out, OP4, not_26_out, not_27_out);
  and and_5 (and_5_out, F14, F13, F12, not_28_out, not_29_out, OP4, not_30_out, not_31_out);
  and and_6 (and_6_out, F14, not_32_out, not_33_out, not_34_out, not_35_out, OP4, not_36_out, not_37_out);
  and and_7 (and_7_out, not_38_out, F13, not_39_out, not_40_out, not_41_out, OP4, not_42_out, not_43_out);
  and and_8 (and_8_out, F30, not_44_out, F14, not_45_out, F12, not_46_out, not_47_out, OP4, not_48_out, not_49_out);
  and and_9 (and_9_out, not_50_out, F25, F14, F13, not_51_out, not_52_out, OP5, OP4, not_53_out, not_54_out);
  and and_10 (and_10_out, F30, not_55_out, not_56_out, not_57_out, not_58_out, not_59_out, OP5, OP4, not_60_out, not_61_out);
  and and_11 (and_11_out, not_62_out, not_63_out, F14, F13, F12, not_64_out, OP5, OP4, not_65_out, not_66_out);
  and and_12 (and_12_out, not_67_out, not_68_out, not_69_out, F13, not_70_out, not_71_out, OP5, OP4, not_72_out, not_73_out);
  and and_13 (and_13_out, F14, F13, F12, not_74_out, not_75_out, OP4, not_76_out, not_77_out);
  and and_14 (and_14_out, not_78_out, F13, not_79_out, not_80_out, not_81_out, OP4, not_82_out, not_83_out);
  and and_15 (and_15_out, not_84_out, not_85_out, F14, not_86_out, F12, not_87_out, not_88_out, OP4, not_89_out, not_90_out);
  and and_16 (and_16_out, not_91_out, not_92_out, not_93_out, not_94_out, not_95_out, not_96_out, OP5, OP4, not_97_out, not_98_out);
  and and_17 (and_17_out, F30, not_99_out, not_100_out, not_101_out, not_102_out, not_103_out, OP5, OP4, not_104_out, not_105_out);
  and and_18 (and_18_out, not_106_out, not_107_out, F14, F13, F12, not_108_out, OP5, OP4, not_109_out, not_110_out);
  and and_19 (and_19_out, not_111_out, not_112_out, not_113_out, F13, F12, not_114_out, OP5, OP4, not_115_out, not_116_out);
  and and_20 (and_20_out, not_117_out, not_118_out, not_119_out, not_120_out, not_121_out, OP4, not_122_out, not_123_out);
  and and_21 (and_21_out, F14, F13, F12, not_124_out, not_125_out, OP4, not_126_out, not_127_out);
  and and_22 (and_22_out, not_128_out, F25, F14, not_129_out, F12, not_130_out, OP5, OP4, not_131_out, not_132_out);
  and and_23 (and_23_out, not_133_out, F25, F14, F13, not_134_out, not_135_out, OP5, OP4, not_136_out, not_137_out);
  and and_24 (and_24_out, F14, F13, not_138_out, OP6, OP5, not_139_out, not_140_out, not_141_out);
  and and_25 (and_25_out, not_142_out, not_143_out, F14, F13, not_144_out, not_145_out, OP5, OP4, not_146_out, not_147_out);
  and and_26 (and_26_out, not_148_out, not_149_out, not_150_out, F13, not_151_out, not_152_out, OP5, OP4, not_153_out, not_154_out);
  and and_27 (and_27_out, not_155_out, not_156_out, not_157_out, F13, F12, not_158_out, OP5, OP4, not_159_out, not_160_out);
  and and_28 (and_28_out, F14, F13, not_161_out, not_162_out, not_163_out, OP4, not_164_out, not_165_out);
  and and_29 (and_29_out, F14, not_166_out, not_167_out, not_168_out, not_169_out, OP4, not_170_out, not_171_out);
  and and_30 (and_30_out, not_172_out, F13, not_173_out, not_174_out, not_175_out, OP4, not_176_out, not_177_out);
  and and_31 (and_31_out, not_178_out, F25, F14, F13, not_179_out, not_180_out, OP5, OP4, not_181_out, not_182_out);
  and and_32 (and_32_out, F14, F13, not_183_out, OP6, OP5, not_184_out, not_185_out, not_186_out);
  or or_1 (S0, and_1_out, and_2_out, and_3_out, and_4_out, and_5_out, and_6_out, and_7_out, and_8_out, and_9_out);
  or or_2 (S1, and_10_out, and_11_out, and_12_out, and_13_out, and_14_out, and_15_out);
  or or_3 (S2, and_16_out, and_17_out, and_18_out, and_19_out, and_20_out, and_21_out, and_22_out, and_23_out, and_24_out);
  or or_4 (S3, and_25_out, and_26_out, and_27_out, and_28_out, and_29_out, and_30_out, and_31_out, and_32_out);
endmodule

// 控制信号生成
module \控制信号自动生成  (
  input  OP2,
  input  OP3,
  input  OP4,
  input  OP5,
  input  OP6,
  input  F12,
  input  F13,
  input  F14,
  input  F25,
  input  F30,
  output MemToReg,
  output MemWrite,
  output ALU_SRC,
  output RegWrite,
  output ecall,
  output S_Type,
  output BEQ,
  output BNE,
  output JALR,
  output JAL,
  output BLTU,
  output Byte
);

  wire and_1_out, and_2_out, and_4_out, and_5_out, and_6_out, and_7_out, and_8_out, and_9_out, and_10_out,
       and_11_out, and_12_out, and_13_out, and_14_out, and_15_out, and_16_out, and_17_out, and_18_out,
       and_19_out, and_20_out, and_21_out, and_22_out, and_23_out, and_24_out, and_25_out, and_26_out,
       and_27_out, and_28_out, and_29_out, and_30_out, and_31_out, and_32_out, and_33_out, and_34_out,
       and_35_out, not_1_out, not_2_out, not_3_out, not_4_out, not_5_out, not_6_out, not_7_out, not_8_out,
       not_9_out, not_10_out, not_11_out, not_12_out, not_13_out, not_14_out, not_15_out, not_16_out,
       not_17_out, not_18_out, not_19_out, not_20_out, not_21_out, not_22_out, not_23_out, not_24_out,
       not_25_out, not_26_out, not_27_out, not_28_out, not_29_out, not_30_out, not_31_out, not_32_out,
       not_33_out, not_34_out, not_35_out, not_36_out, not_37_out, not_38_out, not_39_out, not_40_out,
       not_41_out, not_42_out, not_43_out, not_44_out, not_45_out, not_46_out, not_47_out, not_48_out,
       not_49_out, not_50_out, not_51_out, not_52_out, not_53_out, not_54_out, not_55_out, not_56_out,
       not_57_out, not_58_out, not_59_out, not_60_out, not_61_out, not_62_out, not_63_out, not_64_out,
       not_65_out, not_66_out, not_67_out, not_68_out, not_69_out, not_70_out, not_71_out, not_72_out,
       not_73_out, not_74_out, not_75_out, not_76_out, not_77_out, not_78_out, not_79_out, not_80_out,
       not_81_out, not_82_out, not_83_out, not_84_out, not_85_out, not_86_out, not_87_out, not_88_out,
       not_89_out, not_90_out, not_91_out, not_92_out, not_93_out, not_94_out, not_95_out, not_96_out,
       not_97_out, not_98_out, not_99_out, not_100_out, not_101_out, not_102_out, not_103_out, not_104_out,
       not_105_out, not_106_out, not_107_out, not_108_out, not_109_out, not_110_out, not_111_out,
       not_112_out, not_113_out, not_114_out, not_115_out, not_116_out, not_117_out, not_118_out,
       not_119_out, not_120_out, not_121_out, not_122_out, not_123_out, not_124_out, not_125_out,
       not_126_out, not_127_out, not_128_out, not_129_out, not_130_out, not_131_out, not_132_out,
       not_133_out, not_134_out, not_135_out, not_136_out, not_137_out, not_138_out, not_139_out,
       not_140_out, not_141_out, not_142_out, not_143_out, not_144_out, not_145_out, not_146_out,
       not_147_out, not_148_out, not_149_out, not_150_out, not_151_out, not_152_out, not_153_out,
       not_154_out, not_155_out, not_156_out, not_157_out, not_158_out, not_159_out, not_160_out,
       not_161_out, not_162_out, not_163_out, not_164_out, not_165_out, not_166_out, not_167_out,
       not_168_out, not_169_out, not_170_out, not_171_out, not_172_out, not_173_out, not_174_out,
       not_175_out, not_176_out, not_177_out, not_178_out, not_179_out, not_180_out, not_181_out,
       not_182_out, not_183_out, not_184_out, not_185_out, not_186_out, not_187_out, not_188_out,
       not_189_out, not_190_out, not_191_out, not_192_out, not_193_out, not_194_out, not_195_out,
       not_196_out, not_197_out, not_198_out, not_199_out, not_200_out, not_201_out, not_202_out,
       not_203_out, not_204_out, not_205_out, not_206_out, not_207_out, not_208_out, not_209_out,
       not_210_out, not_211_out, not_212_out, not_213_out, not_214_out, not_215_out, not_216_out,
       not_217_out, not_218_out, not_219_out, not_220_out, not_221_out, not_222_out, not_223_out,
       not_224_out, not_225_out, not_226_out, not_227_out, not_228_out, not_229_out, not_230_out,
       not_231_out, not_232_out, not_233_out, not_234_out, not_235_out, not_236_out, not_237_out,
       not_238_out, not_239_out, not_240_out, not_241_out, not_242_out, not_243_out, not_244_out,
       not_245_out, not_246_out, not_247_out;

  not not_1 (not_1_out, F14);
  not not_2 (not_2_out, F12);
  not not_3 (not_3_out, OP6);
  not not_4 (not_4_out, OP5);
  not not_5 (not_5_out, OP4);
  not not_6 (not_6_out, OP3);
  not not_7 (not_7_out, OP2);
  not not_8 (not_8_out, F13);
  not not_9 (not_9_out, F12);
  not not_10 (not_10_out, OP6);
  not not_11 (not_11_out, OP5);
  not not_12 (not_12_out, OP4);
  not not_13 (not_13_out, OP3);
  not not_14 (not_14_out, OP2);
  not not_15 (not_15_out, F14);
  not not_16 (not_16_out, F12);
  not not_17 (not_17_out, OP6);
  not not_18 (not_18_out, OP4);
  not not_19 (not_19_out, OP3);
  not not_20 (not_20_out, OP2);
  not not_21 (not_21_out, F14);
  not not_22 (not_22_out, F13);
  not not_23 (not_23_out, F12);
  not not_24 (not_24_out, OP6);
  not not_25 (not_25_out, OP5);
  not not_26 (not_26_out, OP3);
  not not_27 (not_27_out, OP2);
  not not_28 (not_28_out, OP6);
  not not_29 (not_29_out, OP5);
  not not_30 (not_30_out, OP3);
  not not_31 (not_31_out, OP2);
  not not_32 (not_32_out, F12);
  not not_33 (not_33_out, OP6);
  not not_34 (not_34_out, OP5);
  not not_35 (not_35_out, OP3);
  not not_36 (not_36_out, OP2);
  not not_37 (not_37_out, F13);
  not not_38 (not_38_out, F12);
  not not_39 (not_39_out, OP6);
  not not_40 (not_40_out, OP5);
  not not_41 (not_41_out, OP3);
  not not_42 (not_42_out, OP2);
  not not_43 (not_43_out, F14);
  not not_44 (not_44_out, F12);
  not not_45 (not_45_out, OP6);
  not not_46 (not_46_out, OP5);
  not not_47 (not_47_out, OP3);
  not not_48 (not_48_out, OP2);
  not not_49 (not_49_out, F14);
  not not_50 (not_50_out, F13);
  not not_51 (not_51_out, OP6);
  not not_52 (not_52_out, OP5);
  not not_53 (not_53_out, OP3);
  not not_54 (not_54_out, OP2);
  not not_55 (not_55_out, F30);
  not not_56 (not_56_out, F25);
  not not_57 (not_57_out, F13);
  not not_58 (not_58_out, OP6);
  not not_59 (not_59_out, OP5);
  not not_60 (not_60_out, OP3);
  not not_61 (not_61_out, OP2);
  not not_62 (not_62_out, F25);
  not not_63 (not_63_out, F13);
  not not_64 (not_64_out, OP6);
  not not_65 (not_65_out, OP5);
  not not_66 (not_66_out, OP3);
  not not_67 (not_67_out, OP2);
  not not_68 (not_68_out, F14);
  not not_69 (not_69_out, F12);
  not not_70 (not_70_out, OP6);
  not not_71 (not_71_out, OP5);
  not not_72 (not_72_out, OP4);
  not not_73 (not_73_out, OP3);
  not not_74 (not_74_out, OP2);
  not not_75 (not_75_out, F14);
  not not_76 (not_76_out, F12);
  not not_77 (not_77_out, OP6);
  not not_78 (not_78_out, OP4);
  not not_79 (not_79_out, OP3);
  not not_80 (not_80_out, OP2);
  not not_81 (not_81_out, F30);
  not not_82 (not_82_out, F12);
  not not_83 (not_83_out, OP6);
  not not_84 (not_84_out, OP3);
  not not_85 (not_85_out, OP2);
  not not_86 (not_86_out, F13);
  not not_87 (not_87_out, F12);
  not not_88 (not_88_out, OP6);
  not not_89 (not_89_out, OP5);
  not not_90 (not_90_out, OP4);
  not not_91 (not_91_out, OP3);
  not not_92 (not_92_out, OP2);
  not not_93 (not_93_out, F30);
  not not_94 (not_94_out, F25);
  not not_95 (not_95_out, F14);
  not not_96 (not_96_out, F13);
  not not_97 (not_97_out, F12);
  not not_98 (not_98_out, OP6);
  not not_99 (not_99_out, OP3);
  not not_100 (not_100_out, OP2);
  not not_101 (not_101_out, F25);
  not not_102 (not_102_out, F14);
  not not_103 (not_103_out, F13);
  not not_104 (not_104_out, F12);
  not not_105 (not_105_out, OP6);
  not not_106 (not_106_out, OP3);
  not not_107 (not_107_out, OP2);
  not not_108 (not_108_out, F30);
  not not_109 (not_109_out, F25);
  not not_110 (not_110_out, OP6);
  not not_111 (not_111_out, OP3);
  not not_112 (not_112_out, OP2);
  not not_113 (not_113_out, F30);
  not not_114 (not_114_out, F25);
  not not_115 (not_115_out, F12);
  not not_116 (not_116_out, OP6);
  not not_117 (not_117_out, OP3);
  not not_118 (not_118_out, OP2);
  not not_119 (not_119_out, F30);
  not not_120 (not_120_out, F25);
  not not_121 (not_121_out, F14);
  not not_122 (not_122_out, F12);
  not not_123 (not_123_out, OP6);
  not not_124 (not_124_out, OP3);
  not not_125 (not_125_out, OP2);
  not not_126 (not_126_out, F30);
  not not_127 (not_127_out, F25);
  not not_128 (not_128_out, F14);
  not not_129 (not_129_out, OP6);
  not not_130 (not_130_out, OP3);
  not not_131 (not_131_out, OP2);
  not not_132 (not_132_out, F14);
  not not_133 (not_133_out, F13);
  not not_134 (not_134_out, F12);
  not not_135 (not_135_out, OP6);
  not not_136 (not_136_out, OP5);
  not not_137 (not_137_out, OP3);
  not not_138 (not_138_out, OP2);
  not not_139 (not_139_out, OP6);
  not not_140 (not_140_out, OP5);
  not not_141 (not_141_out, OP3);
  not not_142 (not_142_out, OP2);
  not not_143 (not_143_out, F12);
  not not_144 (not_144_out, OP6);
  not not_145 (not_145_out, OP5);
  not not_146 (not_146_out, OP3);
  not not_147 (not_147_out, OP2);
  not not_148 (not_148_out, F13);
  not not_149 (not_149_out, F12);
  not not_150 (not_150_out, OP6);
  not not_151 (not_151_out, OP5);
  not not_152 (not_152_out, OP3);
  not not_153 (not_153_out, OP2);
  not not_154 (not_154_out, F14);
  not not_155 (not_155_out, F12);
  not not_156 (not_156_out, OP6);
  not not_157 (not_157_out, OP5);
  not not_158 (not_158_out, OP3);
  not not_159 (not_159_out, OP2);
  not not_160 (not_160_out, F14);
  not not_161 (not_161_out, F13);
  not not_162 (not_162_out, OP6);
  not not_163 (not_163_out, OP5);
  not not_164 (not_164_out, OP3);
  not not_165 (not_165_out, OP2);
  not not_166 (not_166_out, F30);
  not not_167 (not_167_out, F25);
  not not_168 (not_168_out, F13);
  not not_169 (not_169_out, OP6);
  not not_170 (not_170_out, OP5);
  not not_171 (not_171_out, OP3);
  not not_172 (not_172_out, OP2);
  not not_173 (not_173_out, F25);
  not not_174 (not_174_out, F13);
  not not_175 (not_175_out, OP6);
  not not_176 (not_176_out, OP5);
  not not_177 (not_177_out, OP3);
  not not_178 (not_178_out, OP2);
  not not_179 (not_179_out, F14);
  not not_180 (not_180_out, F12);
  not not_181 (not_181_out, OP6);
  not not_182 (not_182_out, OP5);
  not not_183 (not_183_out, OP4);
  not not_184 (not_184_out, OP3);
  not not_185 (not_185_out, OP2);
  not not_186 (not_186_out, OP4);
  not not_187 (not_187_out, F14);
  not not_188 (not_188_out, F13);
  not not_189 (not_189_out, F12);
  not not_190 (not_190_out, OP4);
  not not_191 (not_191_out, OP3);
  not not_192 (not_192_out, F30);
  not not_193 (not_193_out, F13);
  not not_194 (not_194_out, OP6);
  not not_195 (not_195_out, OP3);
  not not_196 (not_196_out, OP2);
  not not_197 (not_197_out, F30);
  not not_198 (not_198_out, F12);
  not not_199 (not_199_out, OP6);
  not not_200 (not_200_out, OP3);
  not not_201 (not_201_out, OP2);
  not not_202 (not_202_out, F13);
  not not_203 (not_203_out, F12);
  not not_204 (not_204_out, OP6);
  not not_205 (not_205_out, OP5);
  not not_206 (not_206_out, OP4);
  not not_207 (not_207_out, OP3);
  not not_208 (not_208_out, OP2);
  not not_209 (not_209_out, F14);
  not not_210 (not_210_out, F13);
  not not_211 (not_211_out, F12);
  not not_212 (not_212_out, OP3);
  not not_213 (not_213_out, OP2);
  not not_214 (not_214_out, F14);
  not not_215 (not_215_out, F12);
  not not_216 (not_216_out, OP6);
  not not_217 (not_217_out, OP4);
  not not_218 (not_218_out, OP3);
  not not_219 (not_219_out, OP2);
  not not_220 (not_220_out, F14);
  not not_221 (not_221_out, F13);
  not not_222 (not_222_out, F12);
  not not_223 (not_223_out, OP4);
  not not_224 (not_224_out, OP3);
  not not_225 (not_225_out, OP2);
  not not_226 (not_226_out, F14);
  not not_227 (not_227_out, F13);
  not not_228 (not_228_out, OP4);
  not not_229 (not_229_out, OP3);
  not not_230 (not_230_out, OP2);
  not not_231 (not_231_out, F14);
  not not_232 (not_232_out, F13);
  not not_233 (not_233_out, F12);
  not not_234 (not_234_out, OP4);
  not not_235 (not_235_out, OP3);
  not not_236 (not_236_out, OP4);
  not not_237 (not_237_out, F12);
  not not_238 (not_238_out, OP4);
  not not_239 (not_239_out, OP3);
  not not_240 (not_240_out, OP2);
  not not_241 (not_241_out, F13);
  not not_242 (not_242_out, F12);
  not not_243 (not_243_out, OP6);
  not not_244 (not_244_out, OP5);
  not not_245 (not_245_out, OP4);
  not not_246 (not_246_out, OP3);
  not not_247 (not_247_out, OP2);
  and and_1 (and_1_out, not_1_out, F13, not_2_out, not_3_out, not_4_out, not_5_out, not_6_out, not_7_out);
  and and_2 (and_2_out, F14, not_8_out, not_9_out, not_10_out, not_11_out, not_12_out, not_13_out, not_14_out);
  and and_3 (MemWrite, not_15_out, F13, not_16_out, not_17_out, OP5, not_18_out, not_19_out, not_20_out);
  and and_4 (and_4_out, not_21_out, not_22_out, not_23_out, not_24_out, not_25_out, OP4, not_26_out, not_27_out);
  and and_5 (and_5_out, F14, F13, F12, not_28_out, not_29_out, OP4, not_30_out, not_31_out);
  and and_6 (and_6_out, F14, F13, not_32_out, not_33_out, not_34_out, OP4, not_35_out, not_36_out);
  and and_7 (and_7_out, F14, not_37_out, not_38_out, not_39_out, not_40_out, OP4, not_41_out, not_42_out);
  and and_8 (and_8_out, not_43_out, F13, not_44_out, not_45_out, not_46_out, OP4, not_47_out, not_48_out);
  and and_9 (and_9_out, not_49_out, not_50_out, F12, not_51_out, not_52_out, OP4, not_53_out, not_54_out);
  and and_10 (and_10_out, not_55_out, not_56_out, F14, not_57_out, F12, not_58_out, not_59_out, OP4, not_60_out, not_61_out);
  and and_11 (and_11_out, F30, not_62_out, F14, not_63_out, F12, not_64_out, not_65_out, OP4, not_66_out, not_67_out);
  and and_12 (and_12_out, not_68_out, F13, not_69_out, not_70_out, not_71_out, not_72_out, not_73_out, not_74_out);
  and and_13 (and_13_out, not_75_out, F13, not_76_out, not_77_out, OP5, not_78_out, not_79_out, not_80_out);
  and and_14 (and_14_out, not_81_out, F25, F14, F13, not_82_out, not_83_out, OP5, OP4, not_84_out, not_85_out);
  and and_15 (and_15_out, F14, not_86_out, not_87_out, not_88_out, not_89_out, not_90_out, not_91_out, not_92_out);
  and and_16 (and_16_out, not_93_out, not_94_out, not_95_out, not_96_out, not_97_out, not_98_out, OP5, OP4, not_99_out, not_100_out);
  and and_17 (and_17_out, F30, not_101_out, not_102_out, not_103_out, not_104_out, not_105_out, OP5, OP4, not_106_out, not_107_out);
  and and_18 (and_18_out, not_108_out, not_109_out, F14, F13, F12, not_110_out, OP5, OP4, not_111_out, not_112_out);
  and and_19 (and_19_out, not_113_out, not_114_out, F14, F13, not_115_out, not_116_out, OP5, OP4, not_117_out, not_118_out);
  and and_20 (and_20_out, not_119_out, not_120_out, not_121_out, F13, not_122_out, not_123_out, OP5, OP4, not_124_out, not_125_out);
  and and_21 (and_21_out, not_126_out, not_127_out, not_128_out, F13, F12, not_129_out, OP5, OP4, not_130_out, not_131_out);
  and and_22 (and_22_out, not_132_out, not_133_out, not_134_out, not_135_out, not_136_out, OP4, not_137_out, not_138_out);
  and and_23 (and_23_out, F14, F13, F12, not_139_out, not_140_out, OP4, not_141_out, not_142_out);
  and and_24 (and_24_out, F14, F13, not_143_out, not_144_out, not_145_out, OP4, not_146_out, not_147_out);
  and and_25 (and_25_out, F14, not_148_out, not_149_out, not_150_out, not_151_out, OP4, not_152_out, not_153_out);
  and and_26 (and_26_out, not_154_out, F13, not_155_out, not_156_out, not_157_out, OP4, not_158_out, not_159_out);
  and and_27 (and_27_out, not_160_out, not_161_out, F12, not_162_out, not_163_out, OP4, not_164_out, not_165_out);
  and and_28 (and_28_out, not_166_out, not_167_out, F14, not_168_out, F12, not_169_out, not_170_out, OP4, not_171_out, not_172_out);
  and and_29 (and_29_out, F30, not_173_out, F14, not_174_out, F12, not_175_out, not_176_out, OP4, not_177_out, not_178_out);
  and and_30 (and_30_out, not_179_out, F13, not_180_out, not_181_out, not_182_out, not_183_out, not_184_out, not_185_out);
  and and_31 (and_31_out, OP6, OP5, not_186_out, OP3, OP2);
  and and_32 (and_32_out, not_187_out, not_188_out, not_189_out, OP6, OP5, not_190_out, not_191_out, OP2);
  and and_33 (and_33_out, not_192_out, F25, F14, not_193_out, F12, not_194_out, OP5, OP4, not_195_out, not_196_out);
  and and_34 (and_34_out, not_197_out, F25, F14, F13, not_198_out, not_199_out, OP5, OP4, not_200_out, not_201_out);
  and and_35 (and_35_out, F14, not_202_out, not_203_out, not_204_out, not_205_out, not_206_out, not_207_out, not_208_out);
  and and_36 (ecall, not_209_out, not_210_out, not_211_out, OP6, OP5, OP4, not_212_out, not_213_out);
  and and_37 (S_Type, not_214_out, F13, not_215_out, not_216_out, OP5, not_217_out, not_218_out, not_219_out);
  and and_38 (BEQ, not_220_out, not_221_out, not_222_out, OP6, OP5, not_223_out, not_224_out, not_225_out);
  and and_39 (BNE, not_226_out, not_227_out, F12, OP6, OP5, not_228_out, not_229_out, not_230_out);
  and and_40 (JALR, not_231_out, not_232_out, not_233_out, OP6, OP5, not_234_out, not_235_out, OP2);
  and and_41 (JAL, OP6, OP5, not_236_out, OP3, OP2);
  and and_42 (BLTU, F14, F13, not_237_out, OP6, OP5, not_238_out, not_239_out, not_240_out);
  and and_43 (Byte, F14, not_241_out, not_242_out, not_243_out, not_244_out, not_245_out, not_246_out, not_247_out);
  or or_1 (MemToReg, and_1_out, and_2_out);
  or or_2 (ALU_SRC, and_4_out, and_5_out, and_6_out, and_7_out, and_8_out, and_9_out, and_10_out, and_11_out, and_12_out, and_13_out, and_14_out, and_15_out);
  or or_3 (RegWrite, and_16_out, and_17_out, and_18_out, and_19_out, and_20_out, and_21_out, and_22_out, and_23_out, and_24_out, and_25_out, and_26_out, and_27_out, and_28_out, and_29_out, and_30_out, and_31_out, and_32_out, and_33_out, and_34_out, and_35_out);
endmodule

// ALU
module ALU (
  input  [31:0] X,
  input  [31:0] Y,
  input  [3:0] AluOP,
  output out_4,
  output Equal,
  output out_6,
  output [31:0] Result,
  output [31:0] Result_2
);

  wire comparator_3_eq, xor_2_out;
  wire [0:0] comparator_1_lt, comparator_2_lt;
  wire [31:0] adder_1_out, AND_out, divider_1_out, divider_1_rem, divider_2_out, divider_2_rem,
       multiplexer_1_out, multiplexer_2_out, multiplexer_3_out, multiplexer_4_out, multiplexer_5_out,
       multiplexer_6_out, multiplexer_7_out, multiplier_1_cout, multiplier_1_out, negator_1_out,
       negator_2_out, negator_3_out, negator_4_out, negator_5_out, NOR_out, OR_out, shifter_1_out,
       shifter_2_out, shifter_3_out, subtractor_1_out, subtractor_2_out, subtractor_3_out, XOR_out;

  assign AND_out = X & Y;  // AND_Gate AND, 32 bits wide
  assign OR_out = X | Y;  // OR_Gate OR, 32 bits wide
  Shifter #(.width(32), .shift("ll")) shifter_1 (.in(X), .\dist (Y[4:0]), .out(shifter_1_out));
  Shifter #(.width(32), .shift("ar")) shifter_2 (.in(X), .\dist (Y[4:0]), .out(shifter_2_out));
  Shifter #(.width(32), .shift("lr")) shifter_3 (.in(X), .\dist (Y[4:0]), .out(shifter_3_out));
  Multiplier #(.width(32)) multiplier_1 (.a(X), .b(Y), .out(multiplier_1_out), .cout(multiplier_1_cout));  // open: cin
  Divider #(.width(32)) divider_1 (.a(X), .b(Y), .out(divider_1_out), .rem(divider_1_rem));  // open: upper
  Adder #(.width(32)) adder_1 (.a(X), .b(Y), .out(adder_1_out));  // open: cin, cout
  Subtractor #(.width(32)) subtractor_1 (.a(X), .b(Y), .out(subtractor_1_out));  // open: bin, bout
  assign XOR_out = X ^ Y;  // XOR_Gate XOR, 32 bits wide
  assign NOR_out = ~(X | Y);  // NOR_Gate NOR, 32 bits wide
  Comparator #(.width(32), .mode("twosComplement")) comparator_1 (
    .a(X), .b(Y), .eq(Equal), .lt(comparator_1_lt[0]));  // open: gt
  Comparator #(.width(32), .mode("unsigned")) comparator_2 (.a(X), .b(Y), .lt(comparator_2_lt[0]));  // open: gt, eq
  Negator #(.width(32)) negator_1 (.in(X), .out(negator_1_out));
  Negator #(.width(32)) negator_2 (.in(Y), .out(negator_2_out));
  Multiplexer #(.select(1), .width(32), .disabled("Z"), .enable("false")) multiplexer_1 (
    .in0(X), .in1(negator_1_out), .out(multiplexer_1_out), .sel(X[31]));
  Multiplexer #(.select(1), .width(32), .disabled("Z"), .enable("false")) multiplexer_2 (
    .in0(Y), .in1(negator_2_out), .out(multiplexer_2_out), .sel(Y[31]));
  Divider #(.width(32)) divider_2 (
    .a(multiplexer_1_out), .b(multiplexer_2_out), .out(divider_2_out), .rem(divider_2_rem));  // open: upper
  Negator #(.width(32)) negator_3 (.in(divider_2_out), .out(negator_3_out));
  Subtractor #(.width(32)) subtractor_2 (
    .a(multiplexer_2_out), .b(divider_2_rem), .out(subtractor_2_out));  // open: bin, bout
  Subtractor #(.width(32)) subtractor_3 (.a(negator_3_out), .b(32'h1), .out(subtractor_3_out));  // open: bin, bout
  Negator #(.width(32)) negator_4 (.in(divider_2_out), .out(negator_4_out));
  Comparator #(.width(32), .mode("twosComplement")) comparator_3 (
    .a(multiplexer_2_out), .b(multiplexer_1_out), .eq(comparator_3_eq));  // open: gt, lt
  Negator #(.width(32)) negator_5 (.in(subtractor_3_out), .out(negator_5_out));
  xor xor_2 (xor_2_out, Y[31], X[31]);
  Multiplexer #(.select(2), .width(32), .disabled("Z"), .enable("false")) multiplexer_3 (
    .in0(divider_2_out), .in1(negator_3_out), .in2(subtractor_3_out), .in3(negator_5_out),
    .out(multiplexer_3_out), .sel({X[31], Y[31]}));
  Multiplexer #(.select(1), .width(32), .disabled("Z"), .enable("false")) multiplexer_4 (
    .in0(multiplexer_3_out), .in1(multiplexer_5_out), .out(multiplexer_4_out), .sel(comparator_3_eq));
  Multiplexer #(.select(1), .width(32), .disabled("Z"), .enable("false")) multiplexer_5 (
    .in0(divider_2_out), .in1(negator_4_out), .out(multiplexer_5_out), .sel(xor_2_out));
  Multiplexer #(.select(1), .width(32), .disabled("Z"), .enable("false")) multiplexer_6 (
    .in0(divider_2_rem), .in1(subtractor_2_out), .out(multiplexer_6_out), .sel(X[31]));
  Multiplexer #(.select(1), .width(32), .disabled("Z"), .enable("false")) multiplexer_7 (
    .in0(multiplexer_6_out), .in1({32{1'b0}}), .out(multiplexer_7_out), .sel(comparator_3_eq));
  Multiplexer #(.select(4), .width(32), .disabled("Z"), .enable("false")) multiplexer_8 (
    .in0(shifter_1_out), .in1(shifter_2_out), .in2(shifter_3_out), .in3(multiplier_1_out),
    .in4(divider_1_out), .in5(adder_1_out), .in6(subtractor_1_out), .in7(AND_out), .in8(OR_out),
    .in9(XOR_out), .in10(NOR_out), .in11({{31{1'b0}}, comparator_1_lt[0]}),
    .in12({{31{1'b0}}, comparator_2_lt[0]}), .in13(multiplexer_4_out), .in14({32{1'b0}}), .in15({32{1'b0}}),
    .out(Result), .sel(AluOP));
  Multiplexer #(.select(4), .width(32), .disabled("Z"), .enable("false")) multiplexer_9 (
    .in0({32{1'b0}}), .in1({32{1'b0}}), .in2({32{1'b0}}), .in3(multiplier_1_cout), .in4(divider_1_rem),
    .in5({32{1'b0}}), .in6({32{1'b0}}), .in7({32{1'b0}}), .in8({32{1'b0}}), .in9({32{1'b0}}),
    .in10({32{1'b0}}), .in11({32{1'b0}}), .in12({32{1'b0}}), .in13(multiplexer_7_out), .in14({32{1'b0}}),
    .in15({32{1'b0}}), .out(Result_2), .sel(AluOP));
  Multiplexer #(.select(4), .width(1), .disabled("Z"), .enable("false")) multiplexer_10 (
    .in0(1'b0), .in1(1'b0), .in2(1'b0), .in3(1'b0), .in4(1'b0), .in5(1'b0), .in6(1'b0), .in7(1'b0),
    .in8(1'b0), .in9(1'b0), .in10(1'b0), .in11(comparator_1_lt[0]), .in12(comparator_2_lt[0]), .in13(1'b0),
    .in14(1'b0), .in15(1'b0), .out(out_6), .sel(AluOP));
  not not_1 (out_4, out_6);

  // Other names for the same wires on the sheet: Result2[31:0] = Result_2; S[3:0] = AluOP; tunnel = out_6;
  //   tunnel_t = out_4

  // Notes on the sheet:
  //   不要改变此引脚区域内容，也不要改变ALU封装形式
  //   输入引脚
  //   输出引脚
endmodule

module Regifile (
  input  [31:0] Din,
  input  Clk,
  input  WE,
  input  [4:0] R1_num,
  input  [4:0] W_num,
  input  [4:0] R2_num,
  output [31:0] R1,
  output [31:0] R2
);

  // RegisterFile registerfile_1: pin names not known; wires that end beside it: Din, Clk, WE, W_num, R1_num, R2_num, R1, R2
endmodule

module \理想流水线  (
  output RegWrite,
  output MemWrite,
  output [31:0] IF_PC,
  output [31:0] ID_PC,
  output [31:0] EX_PC,
  output [31:0] M_PC,
  output [31:0] WB_PC,
  output [31:0] RDin,
  output [31:0] MDin,
  output [31:0] LedData
);

  wire and_1_out, and_2_out, CLK, clock_2_out, comparator_1_eq, comparator_2_eq, comparator_2_lt,
       controlled_buffer_1_out, d_ff_1_q, ecall, EX_MEM_halt_2, EX_MEM_memtoreg_2, EX_MEM_regwrite_2, Go,
       halt, ID_EX_alu_src_2, ID_EX_beq_2, ID_EX_bltu_2, ID_EX_bne_2, ID_EX_byte_2, ID_EX_halt_2,
       ID_EX_jal_2, ID_EX_jalr_2, ID_EX_memtoreg_2, ID_EX_memwrite_2, ID_EX_regwrite_2, ID_EX_s_type_2, IR1,
       IR2, IR3, MEM_WB_memtoreg_2, nand_1_out, not_1_out, not_2_out, not_3_out, RST, Run, W1, W2, W3,
       \单周期硬布线控制器_1_alu_src , \单周期硬布线控制器_1_beq , \单周期硬布线控制器_1_bltu , \单周期硬布线控制器_1_bne , \单周期硬布线控制器_1_byte ,
       \单周期硬布线控制器_1_jal , \单周期硬布线控制器_1_jalr , \单周期硬布线控制器_1_memtoreg , \单周期硬布线控制器_1_memwrite ,
       \单周期硬布线控制器_1_regwrite , \单周期硬布线控制器_1_s_type ;
  wire [3:0] ID_EX_alu_op_2, \单周期硬布线控制器_1_alu_op ;
  wire [4:0] EX_MEM_w_num_2, ID_EX_funct_2, ID_EX_op_2, ID_EX_w_num_2, multiplexer_1_out, multiplexer_2_out,
       W_num;
  wire [12:0] CNT_num;
  wire [15:0] \LoadUse次数 , \总周期数 , \插入气泡数 , \无条件分支数 , \条件分支成功数 ;
  wire [31:0] alu_1_result, bit_extender_1_out, bit_extender_2_out, bit_extender_3_out, bit_extender_4_out,
       branch_PC, EX_IR, EX_MEM_result_2, ID_EX_b_imm12_2, ID_EX_r1_2, ID_EX_r2_2, ID_EX_signimm_2, ID_IR,
       IF_IR, MEM_IR, MEM_WB_aluresult_2, MEM_WB_rd_2, multiplexer_3_out, multiplexer_4_out, PC_4, R1, R2,
       ram_1_data, shifter_1_out, WB_IR;

  Button \u_总复位  (.out(RST));
  Button _1 (.out(IR1));
  Button _2 (.out(IR2));
  Button _3 (.out(IR3));
  // Probe on \总周期数 
  // Probe on \总周期数 
  Button \u_继续运行  (.out(Go));
  LED #(.active("true")) led_1 (.in(W1));
  LED #(.active("true")) led_2 (.in(W2));
  LED #(.active("true")) led_3 (.in(W3));
  Hex_Digit_Display hex_digit_display_1 (.value(LedData[31:28]));  // open: dp
  // Probe on IF_PC[19:0]
  // RiscV_Probe riscv_probe_1: pin names not known; wires that end beside it: IF_IR
  Hex_Digit_Display hex_digit_display_2 (.value(LedData[27:24]));  // open: dp
  Hex_Digit_Display hex_digit_display_3 (.value(LedData[23:20]));  // open: dp
  // Probe on ID_PC[19:0]
  // RiscV_Probe riscv_probe_2: pin names not known; wires that end beside it: ID_IR
  Register #(.width(32), .trigger("rising"), .Select("low")) PC (.D(PC_4), .en(Run), .Q(IF_PC), .clk(CLK), .clr(RST));
  Hex_Digit_Display hex_digit_display_4 (.value(LedData[15:12]));  // open: dp
  Hex_Digit_Display hex_digit_display_5 (.value(LedData[19:16]));  // open: dp
  Adder #(.width(32)) adder_1 (.a(IF_PC), .b(32'h4), .out(PC_4));  // open: cin, cout
  Hex_Digit_Display hex_digit_display_6 (.value(LedData[7:4]));  // open: dp
  Hex_Digit_Display hex_digit_display_7 (.value(LedData[11:8]));  // open: dp
  Clock #(.highDuration(1), .lowDuration(1)) clock_1 (.out(CLK));
  // Probe on EX_PC[19:0]
  // RiscV_Probe riscv_probe_3: pin names not known; wires that end beside it: EX_IR
  ROM #(.addrWidth(10), .dataWidth(32), .Select("high")) rom_1 (.addr(IF_PC[11:2]), .data(IF_IR));
  Hex_Digit_Display hex_digit_display_8 (.value(LedData[3:0]));  // open: dp
  IF_ID IF_ID (.\指令字 (IF_IR), .PC(IF_PC), .\指令字_2 (ID_IR), .PC_2(ID_PC), .CLK(CLK), .Run(Run), .RST(1'b0));
  // Probe on \总周期数 
  // Probe on M_PC[19:0]
  // RiscV_Probe riscv_probe_4: pin names not known; wires that end beside it: MEM_IR
  // Probe on \总周期数 
  // Probe on \无条件分支数 
  // Probe on \条件分支成功数 
  // Probe on \插入气泡数 
  // Probe on \LoadUse次数 
  assign bit_extender_1_out = {{20{ID_IR[31]}}, ID_IR[31:20]};  // Bit_Extender bit_extender_1
  assign bit_extender_2_out = {{20{ID_IR[31]}}, {ID_IR[31:25], ID_IR[11:7]}};  // Bit_Extender bit_extender_2
  // Probe on IF_PC[11:0]
  // Probe on WB_PC[19:0]
  // RiscV_Probe riscv_probe_5: pin names not known; wires that end beside it: WB_IR
  \单周期硬布线控制器  \u_单周期硬布线控制器_1  (
    .Funct({ID_IR[30], ID_IR[25], ID_IR[14:12]}), .OP(ID_IR[6:2]), .ALU_OP(\单周期硬布线控制器_1_alu_op ),
    .MemToReg(\单周期硬布线控制器_1_memtoreg ), .MemWrite(\单周期硬布线控制器_1_memwrite ), .ALU_SRC(\单周期硬布线控制器_1_alu_src ),
    .RegWrite(\单周期硬布线控制器_1_regwrite ), .ecall(ecall), .S_type(\单周期硬布线控制器_1_s_type ),
    .Jalr(\单周期硬布线控制器_1_jalr ), .Beq(\单周期硬布线控制器_1_beq ), .JAL(\单周期硬布线控制器_1_jal ), .Bne(\单周期硬布线控制器_1_bne ),
    .Bltu(\单周期硬布线控制器_1_bltu ), .Byte(\单周期硬布线控制器_1_byte ));
  Multiplexer #(.select(1), .width(5), .disabled("Z"), .enable("false")) multiplexer_1 (
    .in0(ID_IR[19:15]), .in1(5'b10001), .out(multiplexer_1_out), .sel(ecall));
  Multiplexer #(.select(1), .width(5), .disabled("Z"), .enable("false")) multiplexer_2 (
    .in0(ID_IR[24:20]), .in1(5'b01010), .out(multiplexer_2_out), .sel(ecall));
  Multiplexer #(.select(1), .width(32), .disabled("Z"), .enable("false")) multiplexer_3 (
    .in0(bit_extender_1_out), .in1(bit_extender_2_out), .out(multiplexer_3_out), .sel(\单周期硬布线控制器_1_s_type ));
  Comparator #(.width(32), .mode("twosComplement")) comparator_1 (
    .a(R1), .b(32'ha), .eq(comparator_1_eq));  // open: gt, lt
  // Probe on EX_PC[11:0]
  // Probe on ID_PC[11:0]
  assign bit_extender_3_out = {{20{ID_IR[31]}}, {ID_IR[31], ID_IR[7], ID_IR[30:25], ID_IR[11:8]}};  // Bit_Extender bit_extender_3
  assign bit_extender_4_out = {{12{ID_IR[31]}}, {ID_IR[31], ID_IR[19:12], ID_IR[20], ID_IR[30:21]}};  // Bit_Extender bit_extender_4
  and and_1 (and_1_out, ecall, not_1_out);
  not not_1 (not_1_out, comparator_1_eq);
  and and_2 (and_2_out, ecall, comparator_1_eq);
  // Probe on M_PC[11:0]
  D_Flip_Flop #(.trigger("high"), .Pre_Clr_Positions("LEGACY"), .NegatePresetClear("false"), .enable("true"), .NewFFLayout("false")) d_ff_1 (.Q(d_ff_1_q));  // open: clk, D, Qn, preset, en, reset
  // Probe on 13'hc
  ID_EX ID_EX (
    .OP(ID_IR[6:2]), .Funct({ID_IR[30], ID_IR[25], ID_IR[14:12]}), .Beq(\单周期硬布线控制器_1_beq ),
    .Bne(\单周期硬布线控制器_1_bne ), .MemWrite(\单周期硬布线控制器_1_memwrite ), .ALU_OP(\单周期硬布线控制器_1_alu_op ),
    .ALU_SRC(\单周期硬布线控制器_1_alu_src ), .RegWrite(\单周期硬布线控制器_1_regwrite ), .S_type(\单周期硬布线控制器_1_s_type ),
    .Jal(\单周期硬布线控制器_1_jal ), .jalr(\单周期硬布线控制器_1_jalr ), .Bltu(\单周期硬布线控制器_1_bltu ), .Byte(\单周期硬布线控制器_1_byte ),
    .Clk(CLK), .OP_2(ID_EX_op_2), .Funct_2(ID_EX_funct_2), .Beq_2(ID_EX_beq_2), .bne_2(ID_EX_bne_2),
    .MemWrite_2(ID_EX_memwrite_2), .ALU_OP_2(ID_EX_alu_op_2), .ALU_SRC_2(ID_EX_alu_src_2),
    .RegWrite_2(ID_EX_regwrite_2), .S_type_2(ID_EX_s_type_2), .Jal_2(ID_EX_jal_2), .Jalr_2(ID_EX_jalr_2),
    .Bltu_2(ID_EX_bltu_2), .Byte_2(ID_EX_byte_2), .MemToReg(\单周期硬布线控制器_1_memtoreg ),
    .MemToReg_2(ID_EX_memtoreg_2), .R1(R1), .R2(R2), .R1_2(ID_EX_r1_2), .R2_2(ID_EX_r2_2),
    .SignImm(multiplexer_3_out), .SignImm_2(ID_EX_signimm_2), .PC(ID_PC), .PC_2(EX_PC), .W_num(ID_IR[11:7]),
    .W_num_2(ID_EX_w_num_2), .Run(Run), .RST(1'b0), .halt(and_2_out), .halt_2(ID_EX_halt_2), .IR(ID_IR),
    .IR_2(EX_IR), .B_Imm12(bit_extender_3_out), .B_Imm12_2(ID_EX_b_imm12_2), .U_Imm20(bit_extender_4_out));  // open: U_Imm20_2, R1Forward, R1Forward_2, R2Forward, R2Forward_2, ecall, ecall_2
  Regifile regifile_1 (
    .Din(RDin), .Clk(CLK), .R1(R1), .R2(R2), .WE(RegWrite), .W_num(W_num), .R1_num(multiplexer_1_out),
    .R2_num(multiplexer_2_out));
  Register #(.width(32), .trigger("rising"), .Select("low")) register_1 (
    .D(R2), .en(and_1_out), .Q(LedData), .clk(CLK), .clr(RST));
  // Probe on WB_PC[11:0]
  Comparator #(.width(13), .mode("twosComplement")) comparator_2 (
    .a(CNT_num), .b(13'hc), .eq(comparator_2_eq), .lt(comparator_2_lt));  // open: gt
  Clock #(.highDuration(1), .lowDuration(1)) clock_2 (.out(clock_2_out));
  nand nand_1 (nand_1_out, d_ff_1_q, comparator_2_eq);
  Counter #(.width(13), .max('h1fff), .ongoal("stay"), .trigger("rising"), .behavior("old")) counter_1 (
    .count(comparator_2_lt), .Q(CNT_num), .clk(clock_2_out));  // open: load, D, carry, clr, preset
  Multiplexer #(.select(1), .width(32), .disabled("Z"), .enable("false")) multiplexer_4 (
    .in0(ID_EX_r2_2), .in1(ID_EX_signimm_2), .out(multiplexer_4_out), .sel(ID_EX_alu_src_2));
  Shifter #(.width(32), .shift("ll")) shifter_1 (.in(ID_EX_b_imm12_2), .\dist (5'b00001), .out(shifter_1_out));
  assign controlled_buffer_1_out = nand_1_out ? clock_2_out : 1'bz;  // Controlled_Buffer controlled_buffer_1
  ALU alu_1 (
    .X(ID_EX_r1_2), .Y(multiplexer_4_out), .AluOP(ID_EX_alu_op_2), .Result(alu_1_result));  // open: Equal, Result_2, out_4, out_6
  Pull_Resistor #(.pull(1)) pull_resistor_1 (.node(controlled_buffer_1_out));
  EX_MEM EX_MEM (
    .OP(ID_EX_op_2), .Funct(ID_EX_funct_2), .Beq(ID_EX_beq_2), .Bne(ID_EX_bne_2),
    .MemToReg(ID_EX_memtoreg_2), .MemWrite(ID_EX_memwrite_2), .ALU_SRC(ID_EX_alu_src_2),
    .RegWrite(ID_EX_regwrite_2), .S_type(ID_EX_s_type_2), .Jal(ID_EX_jal_2), .jalr(ID_EX_jalr_2),
    .Bltu(ID_EX_bltu_2), .Byte(ID_EX_byte_2), .Result(alu_1_result), .WriteData(ID_EX_r2_2), .PC(EX_PC),
    .MemToReg_2(EX_MEM_memtoreg_2), .MemWrite_2(MemWrite), .RegWrite_2(EX_MEM_regwrite_2),
    .Result_2(EX_MEM_result_2), .WriteData_2(MDin), .PC_2(M_PC), .Clk(CLK), .W_num(ID_EX_w_num_2),
    .W_num_2(EX_MEM_w_num_2), .Run(Run), .halt(ID_EX_halt_2), .halt_2(EX_MEM_halt_2), .RST(RST), .IR(EX_IR),
    .IR_2(MEM_IR));  // open: ALU_OP, OP_2, Funct_2, Beq_2, bne_2, ALU_OP_2, ALU_SRC_2, S_type_2, Jal_2, Jalr_2, Bltu_2, Byte_2, equal_2, equal, B_Imm12_2, U_Imm20, U_Imm20_2, B_Imm12
  Adder #(.width(32)) adder_2 (.a(shifter_1_out), .b(EX_PC), .out(branch_PC));  // open: cin, cout
  not not_2 (not_2_out, halt);
  Counter #(.width(16), .max('hffff), .ongoal("wrap"), .trigger("rising"), .behavior("new")) counter_2 (
    .count(not_2_out), .Q(\总周期数 ), .clk(CLK));  // open: load, D, carry, clr, preset, down
  not not_3 (not_3_out, halt);
  MEM_WB MEM_WB (
    .RegWrite(EX_MEM_regwrite_2), .MemToReg(EX_MEM_memtoreg_2), .AluResult(EX_MEM_result_2), .RD(ram_1_data),
    .PC(M_PC), .RegWrite_2(RegWrite), .MemToReg_2(MEM_WB_memtoreg_2), .AluResult_2(MEM_WB_aluresult_2),
    .RD_2(MEM_WB_rd_2), .PC_2(WB_PC), .Clk(CLK), .W_num(EX_MEM_w_num_2), .W_num_2(W_num), .Run(Run),
    .halt(EX_MEM_halt_2), .halt_2(halt), .RST(RST), .IR(MEM_IR), .IR_2(WB_IR));  // open: Jal, Jal_2, jalr, Jalr_2, Bltu, Bltu_2, Byte, Byte_2
  RAM #(.addrWidth(10), .dataWidth(32), .bus("separate"), .Select("high")) ram_1 (
    .addr(EX_MEM_result_2[11:2]), .din(MDin), .data(ram_1_data), .str(MemWrite), .clk(CLK),
    .ld(EX_MEM_memtoreg_2));  // open: sel, clr
  or or_1 (Run, Go, not_3_out);
  Multiplexer #(.select(1), .width(32), .disabled("Z"), .enable("false")) multiplexer_5 (
    .in0(MEM_WB_aluresult_2), .in1(MEM_WB_rd_2), .out(RDin), .sel(MEM_WB_memtoreg_2));

  // Other names for the same wires on the sheet: MEM_PC[31:0] = M_PC

  // Notes on the sheet:
  //   中断源
  //   时空图监测，可删除
  //   中断等待指示
  //   数码管输出
  //   指令存储器
  //   contents of rom_1 (hex, n*v repeats v):
  //   413 493 913 993 46413 14e493 296913 39e993 842023 942223 1242423 1342623 a00893 493 913 993 73
  //   指令字
  //   控制位
  //   流水调试日志用
  //   暂停节拍，不能为0
  //   戳工具置1进入计数暂停模式，ctrl+k时钟自动运行到对应节拍暂停
  //   ctrl+k关闭时钟连续运行，将控制位置零，进入单步调试模式调试
  //   用这个时钟源需要去掉电路中的其他时钟源
  //   可计数暂停的时钟源
  //   为方便自动评测，需要输出流水线各段保存的PC值，注意是PC不是PC+4，另外ID段寄存器写入信息，Mem段内存写入信息也要输出
endmodule

module \气泡流水线  (
  output RegWrite,
  output MemWrite,
  output [31:0] IF_PC,
  output [31:0] ID_PC,
  output [31:0] EX_PC,
  output [31:0] M_PC,
  output [31:0] WB_PC,
  output [31:0] RDin,
  output [31:0] MDin,
  output [31:0] LedData
);

  wire alu_1_equal, alu_1_out_6, ALU_SRC, and_1_out, and_2_out, and_3_out, and_4_out, and_5_out, and_6_out,
       and_7_out, and_8_out, and_9_out, and_10_out, and_11_out, and_12_out, and_13_out, and_14_out,
       and_15_out, and_16_out, bjmp, branch, CLK, clock_2_out, comparator_1_eq, comparator_2_eq,
       comparator_2_lt, comparator_3_eq, comparator_4_eq, comparator_5_eq, comparator_6_eq, comparator_7_eq,
       comparator_8_eq, comparator_9_eq, comparator_10_eq, comparator_11_eq, controlled_buffer_1_out,
       d_ff_1_q, DataHazzard, EX_MEM_bltu_2, EX_MEM_byte_2, EX_MEM_halt_2, EX_MEM_jal_2, EX_MEM_jalr_2,
       EX_MEM_memtoreg_2, EX_RegWrite, EX_S_type, Go, halt, ID_EX_alu_src_2, ID_EX_beq_2, ID_EX_bltu_2,
       ID_EX_bne_2, ID_EX_byte_2, ID_EX_halt_2, ID_EX_memtoreg_2, ID_EX_memwrite_2, ID_S_type, IR1, IR2, IR3,
       jal, jalr, MEM_RegWrite, MEM_S_type, MEM_WB_byte_2, MEM_WB_jal_2, MEM_WB_jalr_2, MEM_WB_memtoreg_2,
       nand_1_out, nor_1_out, nor_2_out, not_1_out, not_2_out, not_3_out, not_4_out, not_5_out, not_6_out,
       not_7_out, not_8_out, not_9_out, not_10_out, not_11_out, not_12_out, not_13_out, or_1_out, or_2_out,
       or_6_out, or_7_out, or_8_out, or_9_out, or_10_out, riscv_probe_2_p2, RST, Run, W1, W2, W3,
       \单周期硬布线控制器_1_beq , \单周期硬布线控制器_1_bltu , \单周期硬布线控制器_1_bne , \单周期硬布线控制器_1_byte , \单周期硬布线控制器_1_ecall ,
       \单周期硬布线控制器_1_jal , \单周期硬布线控制器_1_jalr , \单周期硬布线控制器_1_memtoreg , \单周期硬布线控制器_1_memwrite ,
       \单周期硬布线控制器_1_regwrite ;
  wire [0:0] adder_2_out;
  wire [1:0] priority_encoder_1_out, priority_encoder_2_out;
  wire [3:0] ID_EX_alu_op_2, \单周期硬布线控制器_1_alu_op ;
  wire [4:0] EX_W_num, ID_EX_funct_2, ID_EX_op_2, MEM_W_num, R1_num, R2_num, W_num;
  wire [7:0] multiplexer_9_out;
  wire [12:0] CNT_num;
  wire [15:0] \LoadUse次数 , \总周期数 , \插入气泡数 , \无条件分支数 , \条件分支成功数 ;
  wire [31:0] alu_1_result, alu_1_result_2, bit_extender_1_out, bit_extender_2_out, bit_extender_3_out,
       bit_extender_4_out, bit_extender_5_out, branch_PC, EX_IR, EX_MEM_result_2, ID_EX_b_imm12_2,
       ID_EX_r1_2, ID_EX_r2_2, ID_EX_signimm_2, ID_EX_u_imm20_2, ID_IR, IF_IR, MEM_IR, MEM_WB_aluresult_2,
       MEM_WB_rd_2, multiplexer_1_out, multiplexer_4_out, multiplexer_5_out, multiplexer_6_out,
       multiplexer_7_out, PC_4, R1, R2, ram_1_data, shifter_1_out, WB_IR, WB_PC_4;
  wire [31:1] jalr_PC;

  Button \u_总复位  (.out(RST));
  Button _1 (.out(IR1));
  Button _2 (.out(IR2));
  Button _3 (.out(IR3));
  // Probe on \总周期数 
  // Probe on \总周期数 
  not not_1 (not_1_out, halt);
  Counter #(.width(16), .max('hffff), .ongoal("wrap"), .trigger("rising"), .behavior("new")) counter_1 (
    .count(not_1_out), .Q(\无条件分支数 ), .clk(or_1_out));  // open: load, D, carry, clr, preset, down
  or or_1 (or_1_out, jal, jalr);
  Button \u_继续运行  (.out(Go));
  LED #(.active("true")) led_1 (.in(W1));
  LED #(.active("true")) led_2 (.in(W2));
  LED #(.active("true")) led_3 (.in(W3));
  Hex_Digit_Display hex_digit_display_1 (.value(LedData[31:28]));  // open: dp
  // Probe on IF_PC[19:0]
  // RiscV_Probe riscv_probe_1: pin names not known; wires that end beside it: IF_IR
  Hex_Digit_Display hex_digit_display_2 (.value(LedData[23:20]));  // open: dp
  Hex_Digit_Display hex_digit_display_3 (.value(LedData[27:24]));  // open: dp
  // Probe on ID_PC[19:0]
  // RiscV_Probe riscv_probe_2: pin names not known; wires that end beside it: ID_IR, riscv_probe_2_p2
  and and_1 (and_1_out, ~halt, CLK);  // AND_Gate
  nor nor_1 (nor_1_out, bjmp, jal, jalr);
  Priority_Encoder #(.select(2), .disabled("Z")) priority_encoder_1 (
    .in0(nor_1_out), .in1(bjmp), .in2(jal), .in3(jalr), .out(priority_encoder_1_out));  // open: gs, en_out, en_in
  Multiplexer #(.select(2), .width(32), .disabled("Z"), .enable("false")) multiplexer_1 (
    .in0(PC_4), .in1(branch_PC), .in2(branch_PC), .in3({jalr_PC, 1'b0}), .out(multiplexer_1_out),
    .sel(priority_encoder_1_out));
  and and_2 (and_2_out, not_2_out, Run);
  not not_2 (not_2_out, DataHazzard);
  Hex_Digit_Display hex_digit_display_4 (.value(LedData[19:16]));  // open: dp
  Hex_Digit_Display hex_digit_display_5 (.value(LedData[15:12]));  // open: dp
  Counter #(.width(16), .max('hffff), .ongoal("wrap"), .trigger("rising"), .behavior("old")) counter_2 (
    .count(bjmp), .Q(\条件分支成功数 ), .clk(and_1_out), .preset(riscv_probe_2_p2));  // open: load, D, carry, clr
  Register #(.width(32), .trigger("rising"), .Select("low")) PC (
    .D(multiplexer_1_out), .en(and_2_out), .Q(IF_PC), .clk(CLK), .clr(RST));
  Hex_Digit_Display hex_digit_display_6 (.value(LedData[11:8]));  // open: dp
  Hex_Digit_Display hex_digit_display_7 (.value(LedData[7:4]));  // open: dp
  Clock #(.highDuration(1), .lowDuration(1)) clock_1 (.out(CLK));
  // Probe on EX_PC[19:0]
  // RiscV_Probe riscv_probe_3: pin names not known; wires that end beside it: EX_IR
  Adder #(.width(32)) adder_1 (.a(IF_PC), .b(32'h4), .out(PC_4));  // open: cin, cout
  Hex_Digit_Display hex_digit_display_8 (.value(LedData[3:0]));  // open: dp
  and and_3 (and_3_out, ~branch, DataHazzard);  // AND_Gate
  // Probe on \总周期数 
  // Probe on M_PC[19:0]
  // RiscV_Probe riscv_probe_4: pin names not known; wires that end beside it: MEM_IR
  Counter #(.width(16), .max('hffff), .ongoal("wrap"), .trigger("rising"), .behavior("old")) counter_3 (
    .count(and_3_out), .Q(\插入气泡数 ), .clk(and_4_out));  // open: load, D, carry, clr, preset
  and and_4 (and_4_out, ~halt, CLK);  // AND_Gate
  ROM #(.addrWidth(10), .dataWidth(32), .Select("high")) rom_1 (.addr(IF_PC[11:2]), .data(IF_IR));
  not not_3 (not_3_out, DataHazzard);
  // Probe on \总周期数 
  // Probe on \无条件分支数 
  // Probe on \条件分支成功数 
  // Probe on \插入气泡数 
  // Probe on \LoadUse次数 
  IF_ID IF_ID (.\指令字 (IF_IR), .PC(IF_PC), .\指令字_2 (ID_IR), .PC_2(ID_PC), .CLK(CLK), .Run(and_5_out), .RST(branch));
  and and_5 (and_5_out, not_3_out, Run);
  // Probe on IF_PC[11:0]
  // Probe on WB_PC[19:0]
  // RiscV_Probe riscv_probe_5: pin names not known; wires that end beside it: WB_IR
  // Probe on ID_PC[11:0]
  // Probe on EX_PC[11:0]
  \单周期硬布线控制器  \u_单周期硬布线控制器_1  (
    .Funct({ID_IR[30], ID_IR[25], ID_IR[14:12]}), .OP(ID_IR[6:2]), .ALU_OP(\单周期硬布线控制器_1_alu_op ),
    .MemToReg(\单周期硬布线控制器_1_memtoreg ), .MemWrite(\单周期硬布线控制器_1_memwrite ), .ALU_SRC(ALU_SRC),
    .RegWrite(\单周期硬布线控制器_1_regwrite ), .ecall(\单周期硬布线控制器_1_ecall ), .S_type(ID_S_type),
    .Jalr(\单周期硬布线控制器_1_jalr ), .Beq(\单周期硬布线控制器_1_beq ), .JAL(\单周期硬布线控制器_1_jal ), .Bne(\单周期硬布线控制器_1_bne ),
    .Bltu(\单周期硬布线控制器_1_bltu ), .Byte(\单周期硬布线控制器_1_byte ));
  Multiplexer #(.select(1), .width(5), .disabled("Z"), .enable("false")) multiplexer_2 (
    .in0(ID_IR[19:15]), .in1(5'b10001), .out(R1_num), .sel(\单周期硬布线控制器_1_ecall ));
  Multiplexer #(.select(1), .width(5), .disabled("Z"), .enable("false")) multiplexer_3 (
    .in0(ID_IR[24:20]), .in1(5'b01010), .out(R2_num), .sel(\单周期硬布线控制器_1_ecall ));
  assign bit_extender_1_out = {{20{ID_IR[31]}}, ID_IR[31:20]};  // Bit_Extender bit_extender_1
  assign bit_extender_2_out = {{20{ID_IR[31]}}, {ID_IR[31:25], ID_IR[11:7]}};  // Bit_Extender bit_extender_2
  Comparator #(.width(32), .mode("twosComplement")) comparator_1 (
    .a(R1), .b(32'h32), .eq(comparator_1_eq));  // open: gt, lt
  // Probe on M_PC[11:0]
  D_Flip_Flop #(.trigger("high"), .Pre_Clr_Positions("LEGACY"), .NegatePresetClear("false"), .enable("true"), .NewFFLayout("false")) d_ff_1 (.Q(d_ff_1_q));  // open: clk, D, Qn, preset, en, reset
  // Probe on 13'hc
  Multiplexer #(.select(1), .width(32), .disabled("Z"), .enable("false")) multiplexer_4 (
    .in0(bit_extender_1_out), .in1(bit_extender_2_out), .out(multiplexer_4_out), .sel(ID_S_type));
  not not_4 (not_4_out, comparator_1_eq);
  // Probe on WB_PC[11:0]
  Comparator #(.width(13), .mode("twosComplement")) comparator_2 (
    .a(CNT_num), .b(13'hc), .eq(comparator_2_eq), .lt(comparator_2_lt));  // open: gt
  Clock #(.highDuration(1), .lowDuration(1)) clock_2 (.out(clock_2_out));
  Regifile regifile_1 (
    .Din(RDin), .Clk(CLK), .R1(R1), .R2(R2), .WE(RegWrite), .W_num(W_num), .R1_num(R1_num), .R2_num(R2_num));
  assign bit_extender_3_out = {{20{ID_IR[31]}}, {ID_IR[31], ID_IR[7], ID_IR[30:25], ID_IR[11:8]}};  // Bit_Extender bit_extender_3
  assign bit_extender_4_out = {{12{ID_IR[31]}}, {ID_IR[31], ID_IR[19:12], ID_IR[20], ID_IR[30:21]}};  // Bit_Extender bit_extender_4
  and and_6 (and_6_out, \单周期硬布线控制器_1_ecall , not_4_out);
  and and_7 (and_7_out, \单周期硬布线控制器_1_ecall , comparator_1_eq);
  nand nand_1 (nand_1_out, d_ff_1_q, comparator_2_eq);
  Counter #(.width(13), .max('h1fff), .ongoal("stay"), .trigger("rising"), .behavior("old")) counter_4 (
    .count(comparator_2_lt), .Q(CNT_num), .clk(clock_2_out));  // open: load, D, carry, clr, preset
  or or_2 (or_2_out, branch, DataHazzard);
  ID_EX ID_EX (
    .OP(ID_IR[6:2]), .Funct({ID_IR[30], ID_IR[25], ID_IR[14:12]}), .Beq(\单周期硬布线控制器_1_beq ),
    .Bne(\单周期硬布线控制器_1_bne ), .MemWrite(\单周期硬布线控制器_1_memwrite ), .ALU_OP(\单周期硬布线控制器_1_alu_op ),
    .ALU_SRC(ALU_SRC), .RegWrite(\单周期硬布线控制器_1_regwrite ), .S_type(ID_S_type), .Jal(\单周期硬布线控制器_1_jal ),
    .jalr(\单周期硬布线控制器_1_jalr ), .Bltu(\单周期硬布线控制器_1_bltu ), .Byte(\单周期硬布线控制器_1_byte ), .Clk(CLK),
    .OP_2(ID_EX_op_2), .Funct_2(ID_EX_funct_2), .Beq_2(ID_EX_beq_2), .bne_2(ID_EX_bne_2),
    .MemWrite_2(ID_EX_memwrite_2), .ALU_OP_2(ID_EX_alu_op_2), .ALU_SRC_2(ID_EX_alu_src_2),
    .RegWrite_2(EX_RegWrite), .S_type_2(EX_S_type), .Jal_2(jal), .Jalr_2(jalr), .Bltu_2(ID_EX_bltu_2),
    .Byte_2(ID_EX_byte_2), .MemToReg(\单周期硬布线控制器_1_memtoreg ), .MemToReg_2(ID_EX_memtoreg_2), .R1(R1),
    .R2(R2), .R1_2(ID_EX_r1_2), .R2_2(ID_EX_r2_2), .SignImm(multiplexer_4_out), .SignImm_2(ID_EX_signimm_2),
    .PC(ID_PC), .PC_2(EX_PC), .W_num(ID_IR[11:7]), .W_num_2(EX_W_num), .Run(Run), .RST(or_2_out),
    .halt(and_7_out), .halt_2(ID_EX_halt_2), .IR(ID_IR), .IR_2(EX_IR), .B_Imm12(bit_extender_3_out),
    .B_Imm12_2(ID_EX_b_imm12_2), .U_Imm20(bit_extender_4_out), .U_Imm20_2(ID_EX_u_imm20_2));  // open: R1Forward, R1Forward_2, R2Forward, R2Forward_2, ecall, ecall_2
  Register #(.width(32), .trigger("rising"), .Select("low")) register_1 (
    .D(R2), .en(and_6_out), .Q(LedData), .clk(CLK), .clr(RST));
  assign controlled_buffer_1_out = nand_1_out ? clock_2_out : 1'bz;  // Controlled_Buffer controlled_buffer_1
  Multiplexer #(.select(1), .width(32), .disabled("Z"), .enable("false")) multiplexer_5 (
    .in0(ID_EX_r2_2), .in1(ID_EX_signimm_2), .out(multiplexer_5_out), .sel(ID_EX_alu_src_2));
  Pull_Resistor #(.pull(1)) pull_resistor_1 (.node(controlled_buffer_1_out));
  and and_8 (and_8_out, ID_EX_beq_2, alu_1_equal);
  ALU alu_1 (
    .X(ID_EX_r1_2), .Y(multiplexer_5_out), .AluOP(ID_EX_alu_op_2), .Equal(alu_1_equal),
    .Result(alu_1_result), .Result_2(alu_1_result_2), .out_6(alu_1_out_6));  // open: out_4
  Multiplexer #(.select(1), .width(32), .disabled("Z"), .enable("false")) multiplexer_6 (
    .in0(ID_EX_b_imm12_2), .in1(ID_EX_u_imm20_2), .out(multiplexer_6_out), .sel(jal));
  or or_3 (bjmp, and_8_out, and_10_out, and_9_out);
  and and_9 (and_9_out, ID_EX_bltu_2, alu_1_out_6);
  and and_10 (and_10_out, ID_EX_bne_2, not_5_out);
  not not_5 (not_5_out, alu_1_equal);
  Comparator #(.width(4), .mode("twosComplement")) comparator_3 (
    .a(ID_EX_alu_op_2), .b(4'b1101), .eq(comparator_3_eq));  // open: gt, lt
  Adder #(.width(32)) adder_2 (
    .a(ID_EX_signimm_2), .b(ID_EX_r1_2), .out({jalr_PC, adder_2_out[0]}));  // open: cin, cout
  Shifter #(.width(32), .shift("ll")) shifter_1 (.in(multiplexer_6_out), .\dist (5'b00001), .out(shifter_1_out));
  Multiplexer #(.select(1), .width(32), .disabled("Z"), .enable("false")) multiplexer_7 (
    .in0(alu_1_result), .in1(alu_1_result_2), .out(multiplexer_7_out), .sel(comparator_3_eq));
  Adder #(.width(32)) adder_3 (.a(shifter_1_out), .b(EX_PC), .out(branch_PC));  // open: cin, cout
  not not_6 (not_6_out, halt);
  Counter #(.width(16), .max('hffff), .ongoal("wrap"), .trigger("rising"), .behavior("new")) counter_5 (
    .count(not_6_out), .Q(\总周期数 ), .clk(CLK));  // open: load, D, carry, clr, preset, down
  EX_MEM EX_MEM (
    .OP(ID_EX_op_2), .Funct(ID_EX_funct_2), .Beq(ID_EX_beq_2), .Bne(ID_EX_bne_2),
    .MemToReg(ID_EX_memtoreg_2), .MemWrite(ID_EX_memwrite_2), .ALU_SRC(ID_EX_alu_src_2),
    .RegWrite(EX_RegWrite), .S_type(EX_S_type), .Jal(jal), .jalr(jalr), .Bltu(ID_EX_bltu_2),
    .Byte(ID_EX_byte_2), .Result(multiplexer_7_out), .WriteData(ID_EX_r2_2), .PC(EX_PC),
    .MemToReg_2(EX_MEM_memtoreg_2), .MemWrite_2(MemWrite), .RegWrite_2(MEM_RegWrite), .S_type_2(MEM_S_type),
    .Jal_2(EX_MEM_jal_2), .Jalr_2(EX_MEM_jalr_2), .Bltu_2(EX_MEM_bltu_2), .Byte_2(EX_MEM_byte_2),
    .Result_2(EX_MEM_result_2), .WriteData_2(MDin), .PC_2(M_PC), .Clk(CLK), .W_num(EX_W_num),
    .W_num_2(MEM_W_num), .Run(Run), .halt(ID_EX_halt_2), .halt_2(EX_MEM_halt_2), .RST(RST), .IR(EX_IR),
    .IR_2(MEM_IR));  // open: ALU_OP, OP_2, Funct_2, Beq_2, bne_2, ALU_OP_2, ALU_SRC_2, equal_2, equal, B_Imm12_2, U_Imm20, U_Imm20_2, B_Imm12
  or or_4 (branch, bjmp, jal, jalr);
  or or_5 (Run, Go, not_7_out);
  not not_7 (not_7_out, halt);
  RAM #(.addrWidth(10), .dataWidth(32), .bus("separate"), .Select("high")) ram_1 (
    .addr(EX_MEM_result_2[11:2]), .din(MDin), .data(ram_1_data), .str(MemWrite), .clk(CLK),
    .ld(EX_MEM_memtoreg_2));  // open: sel, clr
  MEM_WB MEM_WB (
    .RegWrite(MEM_RegWrite), .MemToReg(EX_MEM_memtoreg_2), .AluResult(EX_MEM_result_2), .RD(ram_1_data),
    .PC(M_PC), .RegWrite_2(RegWrite), .MemToReg_2(MEM_WB_memtoreg_2), .AluResult_2(MEM_WB_aluresult_2),
    .RD_2(MEM_WB_rd_2), .PC_2(WB_PC), .Clk(CLK), .W_num(MEM_W_num), .W_num_2(W_num), .Run(Run),
    .halt(EX_MEM_halt_2), .halt_2(halt), .RST(RST), .IR(MEM_IR), .IR_2(WB_IR), .Jal(EX_MEM_jal_2),
    .Jal_2(MEM_WB_jal_2), .jalr(EX_MEM_jalr_2), .Jalr_2(MEM_WB_jalr_2), .Bltu(EX_MEM_bltu_2),
    .Byte(EX_MEM_byte_2), .Byte_2(MEM_WB_byte_2));  // open: Bltu_2
  nor nor_2 (nor_2_out, MEM_WB_memtoreg_2, MEM_WB_byte_2, or_6_out);
  Priority_Encoder #(.select(2), .disabled("Z")) priority_encoder_2 (
    .in0(nor_2_out), .in1(MEM_WB_memtoreg_2), .in2(or_6_out), .in3(MEM_WB_byte_2),
    .out(priority_encoder_2_out));  // open: gs, en_out, en_in
  Adder #(.width(32)) adder_4 (.a(WB_PC), .b(32'h4), .out(WB_PC_4));  // open: cin, cout
  or or_6 (or_6_out, MEM_WB_jal_2, MEM_WB_jalr_2);
  Multiplexer #(.select(2), .width(32), .disabled("Z"), .enable("false")) multiplexer_8 (
    .in0(MEM_WB_aluresult_2), .in1(MEM_WB_rd_2), .in2(WB_PC_4), .in3(bit_extender_5_out), .out(RDin),
    .sel(priority_encoder_2_out));
  Multiplexer #(.select(2), .width(8), .disabled("Z"), .enable("false")) multiplexer_9 (
    .in0(MEM_WB_rd_2[7:0]), .in1(MEM_WB_rd_2[15:8]), .in2(MEM_WB_rd_2[23:16]), .in3(MEM_WB_rd_2[31:24]),
    .out(multiplexer_9_out), .sel(MEM_WB_aluresult_2[1:0]));
  assign bit_extender_5_out = {{24{1'b0}}, multiplexer_9_out};  // Bit_Extender bit_extender_5
  not not_8 (not_8_out, ALU_SRC);
  not not_9 (not_9_out, ALU_SRC);
  Comparator #(.width(5), .mode("twosComplement")) comparator_4 (
    .a(R1_num), .b(EX_W_num), .eq(comparator_4_eq));  // open: gt, lt
  not not_10 (not_10_out, comparator_5_eq);
  Comparator #(.width(5), .mode("twosComplement")) comparator_5 (
    .a(R1_num), .b({5{1'b0}}), .eq(comparator_5_eq));  // open: gt, lt
  Comparator #(.width(5), .mode("twosComplement")) comparator_6 (
    .a(R2_num), .b(EX_W_num), .eq(comparator_6_eq));  // open: gt, lt
  Comparator #(.width(5), .mode("twosComplement")) comparator_7 (
    .a(R2_num), .b({5{1'b0}}), .eq(comparator_7_eq));  // open: gt, lt
  not not_11 (not_11_out, comparator_7_eq);
  or or_7 (or_7_out, not_8_out, ID_S_type);
  Comparator #(.width(5), .mode("twosComplement")) comparator_8 (
    .a(R1_num), .b(MEM_W_num), .eq(comparator_8_eq));  // open: gt, lt
  Comparator #(.width(5), .mode("twosComplement")) comparator_9 (
    .a(R1_num), .b({5{1'b0}}), .eq(comparator_9_eq));  // open: gt, lt
  not not_12 (not_12_out, comparator_9_eq);
  Comparator #(.width(5), .mode("twosComplement")) comparator_10 (
    .a(R2_num), .b(MEM_W_num), .eq(comparator_10_eq));  // open: gt, lt
  not not_13 (not_13_out, comparator_11_eq);
  Comparator #(.width(5), .mode("twosComplement")) comparator_11 (
    .a(R2_num), .b({5{1'b0}}), .eq(comparator_11_eq));  // open: gt, lt
  or or_8 (or_8_out, not_9_out, ID_S_type);
  and and_11 (and_11_out, comparator_4_eq, not_10_out);
  and and_12 (and_12_out, comparator_6_eq, not_11_out, or_7_out);
  and and_13 (and_13_out, comparator_8_eq, not_12_out);
  and and_14 (and_14_out, comparator_10_eq, not_13_out, or_8_out);
  or or_9 (or_9_out, and_11_out, and_12_out);
  or or_10 (or_10_out, and_13_out, and_14_out);
  and and_15 (and_15_out, EX_RegWrite, or_9_out);
  and and_16 (and_16_out, or_10_out, MEM_RegWrite);
  or or_11 (DataHazzard, and_15_out, and_16_out);

  // Other names for the same wires on the sheet: MEM_PC[31:0] = M_PC

  // Notes on the sheet:
  //   中断源
  //   时空图监测，可删除
  //   中断等待指示
  //   数码管输出
  //   指令存储器
  //   指令字
  //   contents of rom_1 (hex, n*v repeats v):
  //   100493 100006f 100493 200913 300993 100006f 100493 200913 300993 100006f 100493 200913 300993
  //   100006f 100493 200913 300993 3c4000ef 100413 100493 1f49493 900533 2200893 73 24d493 48463 fedff06f
  //   900533 2200893 73 100493 249493 900533 2200893 73 48463 fedff06f 100493 1f49493 900533 2200893 73
  //   4034d493 900533 2200893 73 4044d493 900533 2200893 73 4044d493 900533 2200893 73 4044d493 900533
  //   2200893 73 4044d493 900533 2200893 73 4044d493 900533 2200893 73 4044d493 900533 2200893 73 4044d493
  //   900533 2200893 73 100413 1f41993 41f9d993 433 c00913 300b13 140413 f47413 800293 100313 499993
  //   89e9b3 1300533 2200893 73 406282b3 fe0294e3 140413 f00f93 1f47433 1c41413 800293 100313 49d993
  //   89e9b3 1300533 2200893 73 406282b3 fe0294e3 1c45413 406b0b33 b0463 f95ff06f 2b3 fff2c293 829293
  //   ff2e293 500533 2200893 73 fff00413 493 84a023 140413 448493 84a023 140413 448493 84a023 140413
  //   448493 84a023 140413 448493 84a023 140413 448493 84a023 140413 448493 84a023 140413 448493 84a023
  //   140413 448493 84a023 140413 448493 84a023 140413 448493 84a023 140413 448493 84a023 140413 448493
  //   84a023 140413 448493 84a023 140413 448493 84a023 140413 448493 84a023 140413 448493 140413 433
  //   3c00493 42983 4aa03 149a2b3 28663 134a023 1442023 ffc48493 fe9412e3 800533 2200893 73 440413 3c00493
  //   fc9416e3 3200893 73 200293 1100493 849493 1148493 1049493 900533 2200893 73 1c00e13 254d4b3 900533
  //   2200893 73 fffe0e13 fe0e16e3 3200893 73 8800493 849493 4848493 8700913 891913 5490913 2997933
  //   1091913 11096913 1200533 2200893 73 3200893 73 313 1000e13 8400493 849493 8348493 400913 891913
  //   490913 849493 8248493 849493 8148493 891913 490913 891913 490913 932023 12484b3 430313 fffe0e13
  //   fe0e18e3 2000e13 313 34483 900533 2200893 73 130313 fffe0e13 fe0e14e3 3200893 73 ff100493 900533
  //   2200893 73 148493 fe9068e3 900533 2200893 73 3200893 73 413 140413 800533 2200893 73 240413 800533
  //   2200893 73 340413 800533 2200893 73 440413 800533 2200893 73 540413 800533 2200893 73 640413 800533
  //   2200893 73 740413 800533 2200893 73 840413 800533 2200893 2200893 73 8067
  //   控制位
  //   流水调试日志用
  //   暂停节拍，不能为0
  //   戳工具置1进入计数暂停模式，ctrl+k时钟自动运行到对应节拍暂停
  //   ctrl+k关闭时钟连续运行，将控制位置零，进入单步调试模式调试
  //   可计数暂停的时钟源
  //   为方便自动评测，需要输出流水线各段保存的PC值，注意是PC不是PC+4，另外ID段寄存器写入信息，Mem段内存写入信息也要输出
endmodule
module \重定向流水线  (
  output RegWrite,
  output MemWrite,
  output [31:0] IF_PC,
  output [31:0] ID_PC,
  output [31:0] EX_PC,
  output [31:0] M_PC,
  output [31:0] WB_PC,
  output [31:0] RDin,
  output [31:0] MDin,
  output [31:0] LedData
);

  wire alu_1_equal, alu_1_out_6, ALU_SRC, and_1_out, and_2_out, and_3_out, and_4_out, and_5_out, and_6_out,
       and_7_out, and_8_out, and_9_out, and_10_out, and_11_out, and_12_out, bjmp, branch, CLK, clock_2_out,
       comparator_1_eq, comparator_2_eq, comparator_2_lt, comparator_3_eq, comparator_4_eq, comparator_5_eq,
       comparator_6_eq, comparator_7_eq, comparator_8_eq, comparator_9_eq, comparator_10_eq,
       comparator_11_eq, comparator_12_eq, comparator_13_eq, comparator_14_eq, comparator_15_eq,
       controlled_buffer_1_out, d_ff_1_q, EX_ecalll, EX_MEM_bltu_2, EX_MEM_byte_2, EX_MEM_halt_2,
       EX_MEM_jal_2, EX_MEM_jalr_2, EX_MEM_memtoreg_2, EX_MemToReg, EX_RegWrite, EX_S_type, Go, halt,
       ID_EX_alu_src_2, ID_EX_beq_2, ID_EX_bltu_2, ID_EX_bne_2, ID_EX_byte_2, ID_EX_memwrite_2, ID_S_type,
       IR1, IR2, IR3, jal, jalr, LoadUse, MEM_RegWrite, MEM_S_type, MEM_WB_byte_2, MEM_WB_jal_2,
       MEM_WB_jalr_2, MEM_WB_memtoreg_2, nand_1_out, nor_1_out, nor_2_out, not_1_out, not_2_out, not_3_out,
       not_4_out, not_5_out, not_6_out, not_7_out, not_8_out, not_9_out, not_10_out, not_11_out, not_12_out,
       not_13_out, not_14_out, not_15_out, not_16_out, not_17_out, not_18_out, or_1_out, or_2_out, or_6_out,
       or_7_out, or_8_out, or_9_out, or_10_out, riscv_probe_2_p1, RST, Run, W1, W2, W3, \单周期硬布线控制器_1_beq ,
       \单周期硬布线控制器_1_bltu , \单周期硬布线控制器_1_bne , \单周期硬布线控制器_1_byte , \单周期硬布线控制器_1_ecall , \单周期硬布线控制器_1_jal ,
       \单周期硬布线控制器_1_jalr , \单周期硬布线控制器_1_memtoreg , \单周期硬布线控制器_1_memwrite , \单周期硬布线控制器_1_regwrite ;
  wire [0:0] adder_2_out;
  wire [1:0] ID_EX_r1forward_2, ID_EX_r2forward_2, priority_encoder_1_out, priority_encoder_2_out, R1Forward,
       R2Forward;
  wire [3:0] ID_EX_alu_op_2, \单周期硬布线控制器_1_alu_op ;
  wire [4:0] EX_W_num, ID_EX_funct_2, ID_EX_op_2, MEM_W_num, R1_num, R2_num, W_num;
  wire [7:0] multiplexer_11_out;
  wire [12:0] CNT_num;
  wire [15:0] \LoadUse次数 , \总周期数 , \无条件分支数 , \条件分支成功数 ;
  wire [31:0] alu_1_result, alu_1_result_2, AluResult, bit_extender_1_out, bit_extender_2_out,
       bit_extender_3_out, bit_extender_4_out, bit_extender_5_out, branch_PC, EX_IR, ID_EX_b_imm12_2,
       ID_EX_r1_2, ID_EX_r2_2, ID_EX_signimm_2, ID_EX_u_imm20_2, ID_IR, IF_IR, MEM_IR, MEM_WB_aluresult_2,
       MEM_WB_rd_2, multiplexer_1_out, multiplexer_4_out, multiplexer_7_out, multiplexer_8_out,
       multiplexer_9_out, PC_4, R1, R2, ram_1_data, regifile_1_r1, regifile_1_r2, shifter_1_out, WB_IR,
       WB_PC_4;
  wire [31:1] jalr_PC;

  Button \u_总复位  (.out(RST));
  Button _1 (.out(IR1));
  Button _2 (.out(IR2));
  Button _3 (.out(IR3));
  // Probe on \总周期数 
  // Probe on \总周期数 
  not not_1 (not_1_out, halt);
  Counter #(.width(16), .max('hffff), .ongoal("wrap"), .trigger("falling"), .behavior("new")) counter_1 (
    .count(not_1_out), .Q(\无条件分支数 ), .clk(or_1_out));  // open: load, D, carry, clr, preset, down
  or or_1 (or_1_out, jal, jalr);
  Button \u_继续运行  (.out(Go));
  LED #(.active("true")) led_1 (.in(W1));
  LED #(.active("true")) led_2 (.in(W2));
  LED #(.active("true")) led_3 (.in(W3));
  Hex_Digit_Display hex_digit_display_1 (.value(LedData[31:28]));  // open: dp
  // Probe on IF_PC[19:0]
  // RiscV_Probe riscv_probe_1: pin names not known; wires that end beside it: IF_IR
  nor nor_1 (nor_1_out, bjmp, jal, jalr);
  Hex_Digit_Display hex_digit_display_2 (.value(LedData[27:24]));  // open: dp
  Hex_Digit_Display hex_digit_display_3 (.value(LedData[23:20]));  // open: dp
  // Probe on ID_PC[19:0]
  // RiscV_Probe riscv_probe_2: pin names not known; wires that end beside it: riscv_probe_2_p1, ID_IR
  Counter #(.width(16), .max('hffff), .ongoal("wrap"), .trigger("rising"), .behavior("old")) counter_2 (
    .count(bjmp), .Q(\条件分支成功数 ), .clk(and_1_out), .preset(riscv_probe_2_p1));  // open: load, D, carry, clr
  and and_1 (and_1_out, ~halt, CLK);  // AND_Gate
  Priority_Encoder #(.select(2), .disabled("Z")) priority_encoder_1 (
    .in0(nor_1_out), .in1(bjmp), .in2(jal), .in3(jalr), .out(priority_encoder_1_out));  // open: gs, en_out, en_in
  Multiplexer #(.select(2), .width(32), .disabled("Z"), .enable("false")) multiplexer_1 (
    .in0(PC_4), .in1(branch_PC), .in2(branch_PC), .in3({jalr_PC, 1'b0}), .out(multiplexer_1_out),
    .sel(priority_encoder_1_out));
  and and_2 (and_2_out, not_2_out, Run);
  not not_2 (not_2_out, LoadUse);
  Hex_Digit_Display hex_digit_display_4 (.value(LedData[19:16]));  // open: dp
  Hex_Digit_Display hex_digit_display_5 (.value(LedData[15:12]));  // open: dp
  Register #(.width(32), .trigger("rising"), .Select("low")) PC (
    .D(multiplexer_1_out), .en(and_2_out), .Q(IF_PC), .clk(CLK), .clr(RST));
  Hex_Digit_Display hex_digit_display_6 (.value(LedData[11:8]));  // open: dp
  Hex_Digit_Display hex_digit_display_7 (.value(LedData[7:4]));  // open: dp
  Clock #(.highDuration(1), .lowDuration(1)) clock_1 (.out(CLK));
  // Probe on EX_PC[19:0]
  // RiscV_Probe riscv_probe_3: pin names not known; wires that end beside it: EX_IR
  and and_3 (and_3_out, ~branch, LoadUse);  // AND_Gate
  Adder #(.width(32)) adder_1 (.a(IF_PC), .b(32'h4), .out(PC_4));  // open: cin, cout
  Hex_Digit_Display hex_digit_display_8 (.value(LedData[3:0]));  // open: dp
  Counter #(.width(16), .max('hffff), .ongoal("wrap"), .trigger("rising"), .behavior("old")) counter_3 (
    .count(and_3_out), .Q(\LoadUse次数 ), .clk(and_4_out));  // open: load, D, carry, clr, preset
  and and_4 (and_4_out, ~halt, CLK);  // AND_Gate
  // Probe on \总周期数 
  // Probe on M_PC[19:0]
  // RiscV_Probe riscv_probe_4: pin names not known; wires that end beside it: MEM_IR
  ROM #(.addrWidth(10), .dataWidth(32), .Select("high")) rom_1 (.addr(IF_PC[11:2]), .data(IF_IR));
  and and_5 (and_5_out, not_3_out, Run);
  not not_3 (not_3_out, LoadUse);
  // Probe on \总周期数 
  // Probe on \无条件分支数 
  // Probe on \条件分支成功数 
  // Probe on \LoadUse次数 
  // Probe on \LoadUse次数 
  IF_ID IF_ID (.\指令字 (IF_IR), .PC(IF_PC), .\指令字_2 (ID_IR), .PC_2(ID_PC), .CLK(CLK), .Run(and_5_out), .RST(branch));
  // Probe on IF_PC[11:0]
  // Probe on WB_PC[19:0]
  // RiscV_Probe riscv_probe_5: pin names not known; wires that end beside it: WB_IR
  assign bit_extender_1_out = {{20{ID_IR[31]}}, ID_IR[31:20]};  // Bit_Extender bit_extender_1
  assign bit_extender_2_out = {{20{ID_IR[31]}}, {ID_IR[31:25], ID_IR[11:7]}};  // Bit_Extender bit_extender_2
  // Probe on EX_PC[11:0]
  // Probe on ID_PC[11:0]
  \单周期硬布线控制器  \u_单周期硬布线控制器_1  (
    .Funct({ID_IR[30], ID_IR[25], ID_IR[14:12]}), .OP(ID_IR[6:2]), .ALU_OP(\单周期硬布线控制器_1_alu_op ),
    .MemToReg(\单周期硬布线控制器_1_memtoreg ), .MemWrite(\单周期硬布线控制器_1_memwrite ), .ALU_SRC(ALU_SRC),
    .RegWrite(\单周期硬布线控制器_1_regwrite ), .ecall(\单周期硬布线控制器_1_ecall ), .S_type(ID_S_type),
    .Jalr(\单周期硬布线控制器_1_jalr ), .Beq(\单周期硬布线控制器_1_beq ), .JAL(\单周期硬布线控制器_1_jal ), .Bne(\单周期硬布线控制器_1_bne ),
    .Bltu(\单周期硬布线控制器_1_bltu ), .Byte(\单周期硬布线控制器_1_byte ));
  Multiplexer #(.select(1), .width(5), .disabled("Z"), .enable("false")) multiplexer_2 (
    .in0(ID_IR[19:15]), .in1(5'b10001), .out(R1_num), .sel(\单周期硬布线控制器_1_ecall ));
  Multiplexer #(.select(1), .width(5), .disabled("Z"), .enable("false")) multiplexer_3 (
    .in0(ID_IR[24:20]), .in1(5'b01010), .out(R2_num), .sel(\单周期硬布线控制器_1_ecall ));
  Comparator #(.width(32), .mode("twosComplement")) comparator_1 (
    .a(R1), .b(32'h32), .eq(comparator_1_eq));  // open: gt, lt
  // Probe on M_PC[11:0]
  D_Flip_Flop #(.trigger("high"), .Pre_Clr_Positions("LEGACY"), .NegatePresetClear("false"), .enable("true"), .NewFFLayout("false")) d_ff_1 (.Q(d_ff_1_q));  // open: clk, D, Qn, preset, en, reset
  // Probe on 13'hc
  Multiplexer #(.select(1), .width(32), .disabled("Z"), .enable("false")) multiplexer_4 (
    .in0(bit_extender_1_out), .in1(bit_extender_2_out), .out(multiplexer_4_out), .sel(ID_S_type));
  assign bit_extender_3_out = {{20{ID_IR[31]}}, {ID_IR[31], ID_IR[7], ID_IR[30:25], ID_IR[11:8]}};  // Bit_Extender bit_extender_3
  assign bit_extender_4_out = {{12{ID_IR[31]}}, {ID_IR[31], ID_IR[19:12], ID_IR[20], ID_IR[30:21]}};  // Bit_Extender bit_extender_4
  and and_6 (and_6_out, EX_ecalll, not_4_out);
  not not_4 (not_4_out, comparator_1_eq);
  and and_7 (and_7_out, EX_ecalll, comparator_1_eq);
  // Probe on WB_PC[11:0]
  Comparator #(.width(13), .mode("twosComplement")) comparator_2 (
    .a(CNT_num), .b(13'hc), .eq(comparator_2_eq), .lt(comparator_2_lt));  // open: gt
  Clock #(.highDuration(1), .lowDuration(1)) clock_2 (.out(clock_2_out));
  Regifile regifile_1 (
    .Din(RDin), .Clk(CLK), .R1(regifile_1_r1), .R2(regifile_1_r2), .WE(RegWrite), .W_num(W_num),
    .R1_num(R1_num), .R2_num(R2_num));
  Register #(.width(32), .trigger("rising"), .Select("low")) register_1 (
    .D(R2), .en(and_6_out), .Q(LedData), .clk(CLK), .clr(RST));
  nand nand_1 (nand_1_out, d_ff_1_q, comparator_2_eq);
  Counter #(.width(13), .max('h1fff), .ongoal("stay"), .trigger("rising"), .behavior("old")) counter_4 (
    .count(comparator_2_lt), .Q(CNT_num), .clk(clock_2_out));  // open: load, D, carry, clr, preset
  or or_2 (or_2_out, branch, LoadUse);
  ID_EX ID_EX (
    .OP(ID_IR[6:2]), .Funct({ID_IR[30], ID_IR[25], ID_IR[14:12]}), .Beq(\单周期硬布线控制器_1_beq ),
    .Bne(\单周期硬布线控制器_1_bne ), .MemWrite(\单周期硬布线控制器_1_memwrite ), .ALU_OP(\单周期硬布线控制器_1_alu_op ),
    .ALU_SRC(ALU_SRC), .RegWrite(\单周期硬布线控制器_1_regwrite ), .S_type(ID_S_type), .Jal(\单周期硬布线控制器_1_jal ),
    .jalr(\单周期硬布线控制器_1_jalr ), .Bltu(\单周期硬布线控制器_1_bltu ), .Byte(\单周期硬布线控制器_1_byte ), .Clk(CLK),
    .OP_2(ID_EX_op_2), .Funct_2(ID_EX_funct_2), .Beq_2(ID_EX_beq_2), .bne_2(ID_EX_bne_2),
    .MemWrite_2(ID_EX_memwrite_2), .ALU_OP_2(ID_EX_alu_op_2), .ALU_SRC_2(ID_EX_alu_src_2),
    .RegWrite_2(EX_RegWrite), .S_type_2(EX_S_type), .Jal_2(jal), .Jalr_2(jalr), .Bltu_2(ID_EX_bltu_2),
    .Byte_2(ID_EX_byte_2), .MemToReg(\单周期硬布线控制器_1_memtoreg ), .MemToReg_2(EX_MemToReg), .R1(regifile_1_r1),
    .R2(regifile_1_r2), .R1_2(ID_EX_r1_2), .R2_2(ID_EX_r2_2), .SignImm(multiplexer_4_out),
    .SignImm_2(ID_EX_signimm_2), .PC(ID_PC), .PC_2(EX_PC), .W_num(ID_IR[11:7]), .W_num_2(EX_W_num),
    .Run(Run), .RST(or_2_out), .IR(ID_IR), .IR_2(EX_IR), .B_Imm12(bit_extender_3_out),
    .B_Imm12_2(ID_EX_b_imm12_2), .U_Imm20(bit_extender_4_out), .U_Imm20_2(ID_EX_u_imm20_2),
    .R1Forward(R1Forward), .R1Forward_2(ID_EX_r1forward_2), .R2Forward(R2Forward),
    .R2Forward_2(ID_EX_r2forward_2), .ecall(\单周期硬布线控制器_1_ecall ), .ecall_2(EX_ecalll));  // open: halt, halt_2
  assign controlled_buffer_1_out = nand_1_out ? clock_2_out : 1'bz;  // Controlled_Buffer controlled_buffer_1
  Multiplexer #(.select(2), .width(32), .disabled("Z"), .enable("false")) multiplexer_5 (
    .in0(ID_EX_r1_2), .in1(RDin), .in2(AluResult), .out(R1), .sel(ID_EX_r1forward_2));  // open: in3
  Multiplexer #(.select(2), .width(32), .disabled("Z"), .enable("false")) multiplexer_6 (
    .in0(ID_EX_r2_2), .in1(RDin), .in2(AluResult), .out(R2), .sel(ID_EX_r2forward_2));  // open: in3
  Pull_Resistor #(.pull(1)) pull_resistor_1 (.node(controlled_buffer_1_out));
  and and_8 (and_8_out, ID_EX_beq_2, alu_1_equal);
  Multiplexer #(.select(1), .width(32), .disabled("Z"), .enable("false")) multiplexer_7 (
    .in0(R2), .in1(ID_EX_signimm_2), .out(multiplexer_7_out), .sel(ID_EX_alu_src_2));
  Multiplexer #(.select(1), .width(32), .disabled("Z"), .enable("false")) multiplexer_8 (
    .in0(ID_EX_b_imm12_2), .in1(ID_EX_u_imm20_2), .out(multiplexer_8_out), .sel(jal));
  or or_3 (bjmp, and_8_out, and_9_out, and_10_out);
  and and_9 (and_9_out, ID_EX_bne_2, not_5_out);
  and and_10 (and_10_out, ID_EX_bltu_2, alu_1_out_6);
  not not_5 (not_5_out, alu_1_equal);
  Comparator #(.width(4), .mode("twosComplement")) comparator_3 (
    .a(ID_EX_alu_op_2), .b(4'b1101), .eq(comparator_3_eq));  // open: gt, lt
  ALU alu_1 (
    .X(R1), .Y(multiplexer_7_out), .AluOP(ID_EX_alu_op_2), .Equal(alu_1_equal), .Result(alu_1_result),
    .Result_2(alu_1_result_2), .out_6(alu_1_out_6));  // open: out_4
  Adder #(.width(32)) adder_2 (.a(ID_EX_signimm_2), .b(R1), .out({jalr_PC, adder_2_out[0]}));  // open: cin, cout
  Shifter #(.width(32), .shift("ll")) shifter_1 (.in(multiplexer_8_out), .\dist (5'b00001), .out(shifter_1_out));
  Adder #(.width(32)) adder_3 (.a(shifter_1_out), .b(EX_PC), .out(branch_PC));  // open: cin, cout
  EX_MEM EX_MEM (
    .OP(ID_EX_op_2), .Funct(ID_EX_funct_2), .Beq(ID_EX_beq_2), .Bne(ID_EX_bne_2), .MemToReg(EX_MemToReg),
    .MemWrite(ID_EX_memwrite_2), .ALU_SRC(ID_EX_alu_src_2), .RegWrite(EX_RegWrite), .S_type(EX_S_type),
    .Jal(jal), .jalr(jalr), .Bltu(ID_EX_bltu_2), .Byte(ID_EX_byte_2), .Result(multiplexer_9_out),
    .WriteData(R2), .PC(EX_PC), .MemToReg_2(EX_MEM_memtoreg_2), .MemWrite_2(MemWrite),
    .RegWrite_2(MEM_RegWrite), .S_type_2(MEM_S_type), .Jal_2(EX_MEM_jal_2), .Jalr_2(EX_MEM_jalr_2),
    .Bltu_2(EX_MEM_bltu_2), .Byte_2(EX_MEM_byte_2), .Result_2(AluResult), .WriteData_2(MDin), .PC_2(M_PC),
    .Clk(CLK), .W_num(EX_W_num), .W_num_2(MEM_W_num), .Run(Run), .halt(and_7_out), .halt_2(EX_MEM_halt_2),
    .RST(RST), .IR(EX_IR), .IR_2(MEM_IR));  // open: ALU_OP, OP_2, Funct_2, Beq_2, bne_2, ALU_OP_2, ALU_SRC_2, equal_2, equal, B_Imm12_2, U_Imm20, U_Imm20_2, B_Imm12
  Multiplexer #(.select(1), .width(32), .disabled("Z"), .enable("false")) multiplexer_9 (
    .in0(alu_1_result), .in1(alu_1_result_2), .out(multiplexer_9_out), .sel(comparator_3_eq));
  not not_6 (not_6_out, halt);
  Counter #(.width(16), .max('hffff), .ongoal("wrap"), .trigger("rising"), .behavior("new")) counter_5 (
    .count(not_6_out), .Q(\总周期数 ), .clk(CLK));  // open: load, D, carry, clr, preset, down
  or or_4 (branch, bjmp, jal, jalr);
  or or_5 (Run, Go, not_7_out);
  not not_7 (not_7_out, halt);
  RAM #(.addrWidth(10), .dataWidth(32), .bus("separate"), .Select("high")) ram_1 (
    .addr(AluResult[11:2]), .din(MDin), .data(ram_1_data), .str(MemWrite), .clk(CLK), .ld(EX_MEM_memtoreg_2));  // open: sel, clr
  MEM_WB MEM_WB (
    .RegWrite(MEM_RegWrite), .MemToReg(EX_MEM_memtoreg_2), .AluResult(AluResult), .RD(ram_1_data), .PC(M_PC),
    .RegWrite_2(RegWrite), .MemToReg_2(MEM_WB_memtoreg_2), .AluResult_2(MEM_WB_aluresult_2),
    .RD_2(MEM_WB_rd_2), .PC_2(WB_PC), .Clk(CLK), .W_num(MEM_W_num), .W_num_2(W_num), .Run(Run),
    .halt(EX_MEM_halt_2), .halt_2(halt), .RST(RST), .IR(MEM_IR), .IR_2(WB_IR), .Jal(EX_MEM_jal_2),
    .Jal_2(MEM_WB_jal_2), .jalr(EX_MEM_jalr_2), .Jalr_2(MEM_WB_jalr_2), .Bltu(EX_MEM_bltu_2),
    .Byte(EX_MEM_byte_2), .Byte_2(MEM_WB_byte_2));  // open: Bltu_2
  not not_8 (not_8_out, ALU_SRC);
  nor nor_2 (nor_2_out, MEM_WB_memtoreg_2, MEM_WB_byte_2, or_6_out);
  Priority_Encoder #(.select(2), .disabled("Z")) priority_encoder_2 (
    .in0(nor_2_out), .in1(MEM_WB_memtoreg_2), .in2(or_6_out), .in3(MEM_WB_byte_2),
    .out(priority_encoder_2_out));  // open: gs, en_out, en_in
  Multiplexer #(.select(2), .width(32), .disabled("Z"), .enable("false")) multiplexer_10 (
    .in0(MEM_WB_aluresult_2), .in1(MEM_WB_rd_2), .in2(WB_PC_4), .in3(bit_extender_5_out), .out(RDin),
    .sel(priority_encoder_2_out));
  Adder #(.width(32)) adder_4 (.a(WB_PC), .b(32'h4), .out(WB_PC_4));  // open: cin, cout
  Comparator #(.width(5), .mode("twosComplement")) comparator_4 (
    .a(R1_num), .b(EX_W_num), .eq(comparator_4_eq));  // open: gt, lt
  Comparator #(.width(5), .mode("twosComplement")) comparator_5 (
    .a(R1_num), .b({5{1'b0}}), .eq(comparator_5_eq));  // open: gt, lt
  Comparator #(.width(5), .mode("twosComplement")) comparator_6 (
    .a(R2_num), .b(EX_W_num), .eq(comparator_6_eq));  // open: gt, lt
  Comparator #(.width(5), .mode("twosComplement")) comparator_7 (
    .a(R2_num), .b({5{1'b0}}), .eq(comparator_7_eq));  // open: gt, lt
  or or_6 (or_6_out, MEM_WB_jal_2, MEM_WB_jalr_2);
  Multiplexer #(.select(2), .width(8), .disabled("Z"), .enable("false")) multiplexer_11 (
    .in0(MEM_WB_rd_2[7:0]), .in1(MEM_WB_rd_2[15:8]), .in2(MEM_WB_rd_2[23:16]), .in3(MEM_WB_rd_2[31:24]),
    .out(multiplexer_11_out), .sel(MEM_WB_aluresult_2[1:0]));
  assign bit_extender_5_out = {{24{1'b0}}, multiplexer_11_out};  // Bit_Extender bit_extender_5
  not not_9 (not_9_out, comparator_5_eq);
  not not_10 (not_10_out, comparator_7_eq);
  or or_7 (or_7_out, not_8_out, ID_S_type);
  and and_11 (and_11_out, comparator_4_eq, not_9_out);
  and and_12 (and_12_out, comparator_6_eq, not_10_out, or_7_out);
  or or_8 (or_8_out, and_11_out, and_12_out);
  and and_13 (LoadUse, EX_MemToReg, or_8_out);
  Comparator #(.width(5), .mode("twosComplement")) comparator_8 (
    .a(R1_num), .b(EX_W_num), .eq(comparator_8_eq));  // open: gt, lt
  Comparator #(.width(5), .mode("twosComplement")) comparator_9 (
    .a(R1_num), .b({5{1'b0}}), .eq(comparator_9_eq));  // open: gt, lt
  Comparator #(.width(5), .mode("twosComplement")) comparator_10 (
    .a(R1_num), .b(MEM_W_num), .eq(comparator_10_eq));  // open: gt, lt
  Comparator #(.width(5), .mode("twosComplement")) comparator_11 (
    .a(R1_num), .b({5{1'b0}}), .eq(comparator_11_eq));  // open: gt, lt
  Comparator #(.width(5), .mode("twosComplement")) comparator_12 (
    .a(R2_num), .b(EX_W_num), .eq(comparator_12_eq));  // open: gt, lt
  Comparator #(.width(5), .mode("twosComplement")) comparator_13 (
    .a(R2_num), .b({5{1'b0}}), .eq(comparator_13_eq));  // open: gt, lt
  not not_11 (not_11_out, ALU_SRC);
  Comparator #(.width(5), .mode("twosComplement")) comparator_14 (
    .a(R2_num), .b(MEM_W_num), .eq(comparator_14_eq));  // open: gt, lt
  Comparator #(.width(5), .mode("twosComplement")) comparator_15 (
    .a(R2_num), .b({5{1'b0}}), .eq(comparator_15_eq));  // open: gt, lt
  not not_12 (not_12_out, ALU_SRC);
  not not_13 (not_13_out, comparator_9_eq);
  not not_14 (not_14_out, comparator_11_eq);
  not not_15 (not_15_out, comparator_13_eq);
  or or_9 (or_9_out, not_11_out, ID_S_type);
  not not_16 (not_16_out, comparator_15_eq);
  or or_10 (or_10_out, not_12_out, ID_S_type);
  and and_14 (R1Forward[1], comparator_8_eq, not_13_out, EX_RegWrite);
  not not_17 (not_17_out, R1Forward[1]);
  and and_15 (R2Forward[1], comparator_12_eq, not_15_out, EX_RegWrite, or_9_out);
  not not_18 (not_18_out, R2Forward[1]);
  and and_16 (R1Forward[0], not_17_out, comparator_10_eq, not_14_out, MEM_RegWrite);
  and and_17 (R2Forward[0], not_18_out, comparator_14_eq, not_16_out, MEM_RegWrite, or_10_out);

  // Other names for the same wires on the sheet: MEM_PC[31:0] = M_PC; 插入气泡数[15:0] = \LoadUse次数 

  // Notes on the sheet:
  //   中断源
  //   中断等待指示
  //   时空图监测，可删除
  //   数码管输出
  //   指令存储器
  //   指令字
  //   contents of rom_1 (hex, n*v repeats v):
  //   100493 100006f 100493 200913 300993 100006f 100493 200913 300993 100006f 100493 200913 300993
  //   100006f 100493 200913 300993 3c4000ef 100413 100493 1f49493 900533 2200893 73 24d493 48463 fedff06f
  //   900533 2200893 73 100493 249493 900533 2200893 73 48463 fedff06f 100493 1f49493 900533 2200893 73
  //   4034d493 900533 2200893 73 4044d493 900533 2200893 73 4044d493 900533 2200893 73 4044d493 900533
  //   2200893 73 4044d493 900533 2200893 73 4044d493 900533 2200893 73 4044d493 900533 2200893 73 4044d493
  //   900533 2200893 73 100413 1f41993 41f9d993 433 c00913 300b13 140413 f47413 800293 100313 499993
  //   89e9b3 1300533 2200893 73 406282b3 fe0294e3 140413 f00f93 1f47433 1c41413 800293 100313 49d993
  //   89e9b3 1300533 2200893 73 406282b3 fe0294e3 1c45413 406b0b33 b0463 f95ff06f 2b3 fff2c293 829293
  //   ff2e293 500533 2200893 73 fff00413 493 84a023 140413 448493 84a023 140413 448493 84a023 140413
  //   448493 84a023 140413 448493 84a023 140413 448493 84a023 140413 448493 84a023 140413 448493 84a023
  //   140413 448493 84a023 140413 448493 84a023 140413 448493 84a023 140413 448493 84a023 140413 448493
  //   84a023 140413 448493 84a023 140413 448493 84a023 140413 448493 84a023 140413 448493 140413 433
  //   3c00493 42983 4aa03 149a2b3 28663 134a023 1442023 ffc48493 fe9412e3 800533 2200893 73 440413 3c00493
  //   fc9416e3 3200893 73 200293 1100493 849493 1148493 1049493 900533 2200893 73 1c00e13 254d4b3 900533
  //   2200893 73 fffe0e13 fe0e16e3 3200893 73 8800493 849493 4848493 8700913 891913 5490913 2997933
  //   1091913 11096913 1200533 2200893 73 3200893 73 313 1000e13 8400493 849493 8348493 400913 891913
  //   490913 849493 8248493 849493 8148493 891913 490913 891913 490913 932023 12484b3 430313 fffe0e13
  //   fe0e18e3 2000e13 313 34483 900533 2200893 73 130313 fffe0e13 fe0e14e3 3200893 73 ff100493 900533
  //   2200893 73 148493 fe9068e3 900533 2200893 73 3200893 73 413 140413 800533 2200893 73 240413 800533
  //   2200893 73 340413 800533 2200893 73 440413 800533 2200893 73 540413 800533 2200893 73 640413 800533
  //   2200893 73 740413 800533 2200893 73 840413 800533 2200893 2200893 73 8067
  //   控制位
  //   流水调试日志用
  //   暂停节拍，不能为0
  //   戳工具置1进入计数暂停模式，ctrl+k时钟自动运行到对应节拍暂停
  //   ctrl+k关闭时钟连续运行，将控制位置零，进入单步调试模式调试
  //   可计数暂停的时钟源
  //   为方便自动评测，需要输出流水线各段保存的PC值，注意是PC不是PC+4，另外ID段寄存器写入信息，Mem段内存写入信息也要输出
endmodule

module \单周期_单级中断  (
  input  IR1,
  input  IR2,
  input  IR3,
  output RegWrite,
  output MemWrite,
  output [31:0] PC,
  output [31:0] IR,
  output [31:0] RDin,
  output [31:0] MDin,
  output [31:0] LedData
);

  wire alu_1_equal, alu_1_out_6, and_3_out, and_4_out, and_5_out, and_6_out, and_7_out, and_8_out,
       and_10_out, and_11_out, Bltu, Byte, CLK, CLR1, CLR2, CLR3, comparator_1_eq, comparator_2_eq,
       comparator_3_eq, comparator_4_eq, comparator_5_eq, comparator_6_eq, comparator_7_eq, d_ff_1_q,
       d_ff_2_q, d_ff_3_q, ecall, Go, halt, IE, INT, INT1, INT2, INT3, into, IR1_t, IR2_t, IR3_t, IR_ecall,
       IRA, IRB, IRC, jal, jalr, jmp, MemToReg, not_1_out, not_2_out, not_3_out, not_4_out, or_5_out,
       or_6_out, or_7_out, or_11_out, or_13_out, pull_resistor_1_node, pull_resistor_2_node,
       pull_resistor_3_node, RST, Run, S_type, uret, W1, W2, W3, \单周期硬布线控制器_1_alu_src , \单周期硬布线控制器_1_beq ,
       \单周期硬布线控制器_1_bne ;
  wire [1:0] adder_1_out, adder_2_out, bit_extender_1_out, multiplexer_3_out, multiplexer_4_out,
       priority_encoder_1_out, register_2_q;
  wire [3:0] AluOP;
  wire [4:0] multiplexer_5_out, multiplexer_6_out;
  wire [7:0] multiplexer_11_out;
  wire [15:0] \总周期数 ;
  wire [31:0] adder_4_out, adder_5_out, adder_6_out, bit_extender_2_out, bit_extender_3_out,
       bit_extender_4_out, bit_extender_5_out, bit_extender_6_out, EPCAddr, INTAddr, multiplexer_2_out,
       multiplexer_7_out, multiplexer_8_out, multiplexer_10_out, PC_4, R1, ram_1_data, Result, Result2,
       RETAddr, shifter_1_out, shifter_2_out;

  Clock #(.highDuration(1), .lowDuration(1)) clock_1 (.out(CLK));
  Button _1 (.out(IRA));
  Button _2 (.out(IRB));
  Button _3 (.out(IRC));
  Button \u_继续运行  (.out(Go));
  LED #(.active("true")) led_1 (.in(W1));
  LED #(.active("true")) led_2 (.in(W2));
  LED #(.active("true")) led_3 (.in(W3));
  Hex_Digit_Display hex_digit_display_1 (.value(LedData[31:28]));  // open: dp
  Multiplexer #(.select(2), .width(32), .disabled("Z"), .enable("false")) multiplexer_1 (
    .in0(PC_4), .in1(adder_4_out), .in2(adder_5_out), .in3({adder_6_out[31:1], 1'b0}), .out(RETAddr),
    .sel(adder_2_out));
  Hex_Digit_Display hex_digit_display_2 (.value(LedData[23:20]));  // open: dp
  Hex_Digit_Display hex_digit_display_3 (.value(LedData[27:24]));  // open: dp
  assign bit_extender_1_out = {{1{1'b0}}, or_11_out};  // Bit_Extender bit_extender_1
  or or_1 (Run, Go, not_1_out);
  not not_1 (not_1_out, halt);
  Multiplexer #(.select(2), .width(32), .disabled("Z"), .enable("false")) multiplexer_2 (
    .in0(RETAddr), .in1(INTAddr), .in2(EPCAddr), .out(multiplexer_2_out), .sel({uret, INT}));  // open: in3
  Hex_Digit_Display hex_digit_display_4 (.value(LedData[19:16]));  // open: dp
  Hex_Digit_Display hex_digit_display_5 (.value(LedData[15:12]));  // open: dp
  Adder #(.width(2)) adder_1 (.a(bit_extender_1_out), .b(multiplexer_3_out), .out(adder_1_out));  // open: cin, cout
  Adder #(.width(2)) adder_2 (.a(adder_1_out), .b(multiplexer_4_out), .out(adder_2_out));  // open: cin, cout
  Register #(.width(32), .trigger("rising"), .Select("low")) u_PC (
    .D(multiplexer_2_out), .en(Run), .Q(PC), .clk(CLK));  // open: clr
  Hex_Digit_Display hex_digit_display_6 (.value(LedData[11:8]));  // open: dp
  Hex_Digit_Display hex_digit_display_7 (.value(LedData[7:4]));  // open: dp
  // Probe on \总周期数 
  Adder #(.width(32)) adder_3 (.a(PC), .b(32'h4), .out(PC_4));  // open: cin, cout
  Comparator #(.width(5), .mode("twosComplement")) comparator_1 (
    .a(IR[24:20]), .b(5'b00010), .eq(comparator_1_eq));  // open: gt, lt
  or or_2 (W1, INT1, d_ff_1_q);
  or or_3 (W2, INT2, d_ff_2_q);
  or or_4 (W3, INT3, d_ff_3_q);
  Hex_Digit_Display hex_digit_display_8 (.value(LedData[3:0]));  // open: dp
  Multiplexer #(.select(1), .width(2), .disabled("Z"), .enable("false")) multiplexer_3 (
    .in0(2'b00), .in1(2'b10), .out(multiplexer_3_out), .sel(jal));
  Multiplexer #(.select(1), .width(2), .disabled("Z"), .enable("false")) multiplexer_4 (
    .in0(2'b00), .in1(2'b11), .out(multiplexer_4_out), .sel(jalr));
  // RiscV_Probe riscv_probe_1: pin names not known; wires that end beside it: RST, IR
  and and_1 (uret, IR_ecall, comparator_1_eq);
  and and_2 (ecall, IR_ecall, ~comparator_1_eq);  // AND_Gate
  D_Flip_Flop #(.trigger("rising"), .Pre_Clr_Positions("LEGACY"), .NegatePresetClear("false"), .enable("true"), .NewFFLayout("false")) d_ff_1 (
    .clk(IRA), .D(1'b1), .Q(d_ff_1_q), .reset(INT1));  // open: Qn, preset, en
  D_Flip_Flop #(.trigger("rising"), .Pre_Clr_Positions("LEGACY"), .NegatePresetClear("false"), .enable("true"), .NewFFLayout("false")) d_ff_2 (
    .clk(IRB), .D(1'b1), .Q(d_ff_2_q), .reset(INT2));  // open: Qn, preset, en
  D_Flip_Flop #(.trigger("rising"), .Pre_Clr_Positions("LEGACY"), .NegatePresetClear("false"), .enable("true"), .NewFFLayout("false")) d_ff_3 (
    .clk(IRC), .D(1'b1), .Q(d_ff_3_q), .reset(INT3));  // open: Qn, preset, en
  and and_3 (and_3_out, into, ~uret);  // AND_Gate
  ROM #(.addrWidth(10), .dataWidth(32), .Select("high")) rom_1 (.addr(PC[11:2]), .data(IR));
  or or_5 (or_5_out, d_ff_1_q, INT1);
  or or_6 (or_6_out, d_ff_2_q, INT2);
  or or_7 (or_7_out, d_ff_3_q, INT3);
  D_Flip_Flop #(.trigger("rising"), .Pre_Clr_Positions("LEGACY"), .NegatePresetClear("false"), .enable("true"), .NewFFLayout("false")) d_ff_4 (
    .clk(CLK), .D(and_3_out), .Q(IE));  // open: Qn, preset, en, reset
  or or_8 (IR1_t, IR1, IRA);
  and and_4 (and_4_out, or_5_out, ~CLR1);  // AND_Gate
  and and_5 (and_5_out, or_6_out, ~CLR2);  // AND_Gate
  and and_6 (and_6_out, or_7_out, ~CLR3);  // AND_Gate
  or or_9 (IR2_t, IR2, IRB);
  \单周期硬布线控制器  \u_单周期硬布线控制器_1  (
    .Funct({IR[30], IR[25], IR[14:12]}), .OP(IR[6:2]), .ALU_OP(AluOP), .MemToReg(MemToReg),
    .MemWrite(MemWrite), .ALU_SRC(\单周期硬布线控制器_1_alu_src ), .RegWrite(RegWrite), .ecall(IR_ecall),
    .S_type(S_type), .Jalr(jalr), .Beq(\单周期硬布线控制器_1_beq ), .JAL(jal), .Bne(\单周期硬布线控制器_1_bne ), .Bltu(Bltu),
    .Byte(Byte));
  assign bit_extender_2_out = {{20{IR[31]}}, {IR[31], IR[7], IR[30:25], IR[11:8]}};  // Bit_Extender bit_extender_2
  assign bit_extender_3_out = {{12{IR[31]}}, {IR[31], IR[19:12], IR[20], IR[30:21]}};  // Bit_Extender bit_extender_3
  Multiplexer #(.select(1), .width(5), .disabled("Z"), .enable("false")) multiplexer_5 (
    .in0(IR[19:15]), .in1(5'b10001), .out(multiplexer_5_out), .sel(ecall));
  Multiplexer #(.select(1), .width(5), .disabled("Z"), .enable("false")) multiplexer_6 (
    .in0(IR[24:20]), .in1(5'b01010), .out(multiplexer_6_out), .sel(ecall));
  assign bit_extender_4_out = {{20{IR[31]}}, IR[31:20]};  // Bit_Extender bit_extender_4
  Shifter #(.width(32), .shift("ll")) shifter_1 (.in(bit_extender_2_out), .\dist (5'b00001), .out(shifter_1_out));
  Shifter #(.width(32), .shift("ll")) shifter_2 (.in(bit_extender_3_out), .\dist (5'b00001), .out(shifter_2_out));
  D_Flip_Flop #(.trigger("rising"), .Pre_Clr_Positions("LEGACY"), .NegatePresetClear("false"), .enable("true"), .NewFFLayout("false")) d_ff_5 (
    .clk(CLK), .D(and_4_out), .Q(INT1));  // open: Qn, preset, en, reset
  D_Flip_Flop #(.trigger("rising"), .Pre_Clr_Positions("LEGACY"), .NegatePresetClear("false"), .enable("true"), .NewFFLayout("false")) d_ff_6 (
    .clk(CLK), .D(and_5_out), .Q(INT2));  // open: Qn, preset, en, reset
  D_Flip_Flop #(.trigger("rising"), .Pre_Clr_Positions("LEGACY"), .NegatePresetClear("false"), .enable("true"), .NewFFLayout("false")) d_ff_7 (
    .clk(CLK), .D(and_6_out), .Q(INT3));  // open: Qn, preset, en, reset
  or or_10 (IR3_t, IR3, IRC);
  or or_11 (or_11_out, and_10_out, and_8_out, and_7_out);
  Regifile regifile_1 (
    .Din(RDin), .Clk(CLK), .R1(R1), .R2(MDin), .WE(RegWrite), .W_num(IR[11:7]), .R1_num(multiplexer_5_out),
    .R2_num(multiplexer_6_out));
  Multiplexer #(.select(1), .width(32), .disabled("Z"), .enable("false")) multiplexer_7 (
    .in0(bit_extender_4_out), .in1(bit_extender_5_out), .out(multiplexer_7_out), .sel(S_type));
  assign bit_extender_5_out = {{20{IR[31]}}, {IR[31:25], IR[11:7]}};  // Bit_Extender bit_extender_5
  Adder #(.width(32)) adder_4 (.a(shifter_1_out), .b(PC), .out(adder_4_out));  // open: cin, cout
  and and_7 (and_7_out, \单周期硬布线控制器_1_bne , not_2_out);
  Multiplexer #(.select(1), .width(32), .disabled("Z"), .enable("false")) multiplexer_8 (
    .in0(MDin), .in1(multiplexer_7_out), .out(multiplexer_8_out), .sel(\单周期硬布线控制器_1_alu_src ));
  Adder #(.width(32)) adder_5 (.a(shifter_2_out), .b(PC), .out(adder_5_out));  // open: cin, cout
  and and_8 (and_8_out, \单周期硬布线控制器_1_beq , alu_1_equal);
  not not_2 (not_2_out, alu_1_equal);
  ALU alu_1 (
    .X(R1), .Y(multiplexer_8_out), .AluOP(AluOP), .Equal(alu_1_equal), .Result(Result), .Result_2(Result2),
    .out_6(alu_1_out_6));  // open: out_4
  Adder #(.width(32)) adder_6 (.a(R1), .b(multiplexer_7_out), .out(adder_6_out));  // open: cin, cout
  and and_9 (INT, into, ~IE);  // AND_Gate
  Register #(.width(32), .trigger("rising"), .Select("low")) register_1 (
    .D(RETAddr), .en(INT), .Q(EPCAddr), .clk(CLK));  // open: clr
  and and_10 (and_10_out, Bltu, alu_1_out_6);
  Priority_Encoder #(.select(2), .disabled("Z")) priority_encoder_1 (
    .in0(INT1), .in1(INT2), .in2(INT3), .out(priority_encoder_1_out), .gs(into));  // open: in3, en_out, en_in
  or or_12 (jmp, jal, jalr);
  not not_3 (not_3_out, comparator_2_eq);
  Comparator #(.width(32), .mode("twosComplement")) comparator_2 (
    .a(R1), .b(32'h32), .eq(comparator_2_eq));  // open: gt, lt
  Comparator #(.width(4), .mode("twosComplement")) comparator_3 (
    .a(AluOP), .b(4'b1101), .eq(comparator_3_eq));  // open: gt, lt
  and and_11 (and_11_out, ecall, not_3_out);
  and and_12 (halt, ecall, comparator_2_eq);
  RAM #(.addrWidth(10), .dataWidth(32), .bus("separate"), .Select("high")) ram_1 (
    .addr(Result[11:2]), .din(MDin), .data(ram_1_data), .str(MemWrite), .clk(CLK), .ld(MemToReg));  // open: sel, clr
  Multiplexer #(.select(2), .width(32), .disabled("Z"), .enable("false")) multiplexer_9 (
    .in0(32'h30ac), .in1(32'h3150), .in2(32'h31f4), .out(INTAddr), .sel(priority_encoder_1_out));  // open: in3
  Register #(.width(2), .trigger("rising"), .Select("low")) register_2 (
    .D(priority_encoder_1_out), .en(INT), .Q(register_2_q), .clk(CLK));  // open: clr
  Multiplexer #(.select(1), .width(32), .disabled("Z"), .enable("false")) multiplexer_10 (
    .in0(Result), .in1(Result2), .out(multiplexer_10_out), .sel(comparator_3_eq));
  Demultiplexer #(.select(2), .width(1), .tristate("false"), .disabled("Z"), .enable("false")) demultiplexer_1 (
    .out0(CLR1), .out1(CLR2), .out2(CLR3), .in(uret), .sel(register_2_q));  // open: out3
  Register #(.width(32), .trigger("rising"), .Select("low")) register_3 (
    .D(MDin), .en(and_11_out), .Q(LedData), .clk(CLK));  // open: clr
  Multiplexer #(.select(2), .width(8), .disabled("Z"), .enable("false")) multiplexer_11 (
    .in0(ram_1_data[7:0]), .in1(ram_1_data[15:8]), .in2(ram_1_data[23:16]), .in3(ram_1_data[31:24]),
    .out(multiplexer_11_out), .sel(Result[1:0]));
  not not_4 (not_4_out, halt);
  Multiplexer #(.select(3), .width(32), .disabled("Z"), .enable("false")) multiplexer_12 (
    .in0(multiplexer_10_out), .in1(ram_1_data), .in2(PC_4), .in5(bit_extender_6_out), .out(RDin),
    .sel({Byte, jmp, MemToReg}));  // open: in3, in4, in6, in7
  assign bit_extender_6_out = {{24{1'b0}}, multiplexer_11_out};  // Bit_Extender bit_extender_6
  Counter #(.width(16), .max('hffff), .ongoal("wrap"), .trigger("rising"), .behavior("new")) counter_1 (
    .count(not_4_out), .Q(\总周期数 ), .clk(CLK));  // open: load, D, carry, clr, preset, down
  Comparator #(.width(16), .mode("twosComplement")) comparator_4 (
    .a(16'h23b), .b(\总周期数 ), .eq(comparator_4_eq));  // open: gt, lt
  or or_13 (or_13_out, comparator_4_eq, comparator_5_eq);
  Comparator #(.width(16), .mode("twosComplement")) comparator_5 (
    .a(\总周期数 ), .b(16'h1), .eq(comparator_5_eq));  // open: gt, lt
  Comparator #(.width(16), .mode("twosComplement")) comparator_6 (
    .a(\总周期数 ), .b(16'h4), .eq(comparator_6_eq));  // open: gt, lt
  Comparator #(.width(16), .mode("twosComplement")) comparator_7 (
    .a(\总周期数 ), .b(16'h7), .eq(comparator_7_eq));  // open: gt, lt
  Pull_Resistor #(.pull(0)) pull_resistor_1 (.node(pull_resistor_1_node));
  assign pull_resistor_1_node = or_13_out ? ~CLK : 1'bz;  // Controlled_Inverter controlled_inverter_1
  Pull_Resistor #(.pull(0)) pull_resistor_2 (.node(pull_resistor_2_node));
  assign pull_resistor_2_node = comparator_6_eq ? ~CLK : 1'bz;  // Controlled_Inverter controlled_inverter_2
  Pull_Resistor #(.pull(0)) pull_resistor_3 (.node(pull_resistor_3_node));
  assign pull_resistor_3_node = comparator_7_eq ? ~CLK : 1'bz;  // Controlled_Inverter controlled_inverter_3

  // Other names for the same wires on the sheet: IR_R2_num[4:0] = IR[24:20]; R2[31:0] = MDin

  // Notes on the sheet:
  //   中断源
  //   中断等待指示
  //   总复位信号应将除ROM以外所有存储组件全部清零
  //   三种分支不同时出现，用加法整合
  //   数码管输出
  //   数码管输出应该用寄存器锁存，否则显示数据只能一闪而过
  //   指令存储器
  //   指令字
  //   contents of rom_1 (hex, n*v repeats v):
  //   7d000113 100413 1f41993 41f9d993 433 c00913 800b13 140413 f47413 800293 100313 499993 89e9b3 1300533
  //   2200893 73 406282b3 fe0294e3 140413 f00f93 1f47433 1c41413 800293 100313 49d993 89e9b3 1300533
  //   2200893 73 406282b3 fe0294e3 1c45413 406b0b33 b0463 f95ff06f 2b3 fff2c293 1029293 fff2e293 500533
  //   2200893 73 f5dff06f 1112023 410113 a12023 410113 812023 410113 1312023 410113 1412023 410113 1512023
  //   410113 1612023 410113 100b13 300a13 100a93 1600433 441413 14469b3 1300533 2200893 73 fe0416e3
  //   415a0a33 fe0a10e3 ffc10113 12b03 ffc10113 12a83 ffc10113 12a03 ffc10113 12983 ffc10113 12403
  //   ffc10113 12503 ffc10113 12883 200073 1112023 410113 a12023 410113 812023 410113 1312023 410113
  //   1412023 410113 1512023 410113 1612023 410113 200b13 300a13 100a93 1600433 441413 14469b3 1300533
  //   2200893 73 fe0416e3 415a0a33 fe0a10e3 ffc10113 12b03 ffc10113 12a83 ffc10113 12a03 ffc10113 12983
  //   ffc10113 12403 ffc10113 12503 ffc10113 12883 200073 1112023 410113 a12023 410113 812023 410113
  //   1312023 410113 1412023 410113 1512023 410113 1612023 410113 300b13 300a13 100a93 1600433 441413
  //   14469b3 1300533 2200893 73 fe0416e3 415a0a33 fe0a10e3 ffc10113 12b03 ffc10113 12a83 ffc10113 12a03
  //   ffc10113 12983 ffc10113 12403 ffc10113 12503 ffc10113 12883 200073
  //   Beq
  //   Bne
  //   MemToReg
  //   MemWrite
  //   AluOP
  //   AluSrcB
  //   RegWrite
  //   jal的目的地址
  //   beq/bne的目的地址
  //   jalr指令的目的地址
  //   为方便自动评测，需要输出PC，IR，寄存器堆写如数据RDin
  //   RAM写使能MemWrite、RAM写入数据MDin等信号
  //   数据存储器
  //   单级中断测试信号模拟器
endmodule

module \中断按键参考电路  (
  input  \同步清零信号 ,
  output \与中断屏蔽位与 
);

  wire \_1号中断_out , and_1_out, clock_1_out, d_ff_1_q, or_1_out, or_2_out;

  Clock #(.highDuration(1), .lowDuration(1)) clock_1 (.out(clock_1_out));
  Button \_1号中断  (.out(\_1号中断_out ));
  LED #(.active("true")) \_1号中断等待指示灯  (.in(or_1_out));
  or or_1 (or_1_out, \与中断屏蔽位与 , d_ff_1_q);
  D_Flip_Flop #(.trigger("rising"), .Pre_Clr_Positions("LEGACY"), .NegatePresetClear("false"), .enable("true"), .NewFFLayout("false")) d_ff_1 (
    .clk(\_1号中断_out ), .D(1'b1), .Q(d_ff_1_q), .reset(\与中断屏蔽位与 ));  // open: Qn, preset, en
  or or_2 (or_2_out, d_ff_1_q, \与中断屏蔽位与 );
  and and_1 (and_1_out, or_2_out, ~\同步清零信号 );  // AND_Gate
  D_Flip_Flop #(.trigger("rising"), .Pre_Clr_Positions("LEGACY"), .NegatePresetClear("false"), .enable("true"), .NewFFLayout("false")) IR1 (
    .clk(clock_1_out), .D(and_1_out), .Q(\与中断屏蔽位与 ));  // open: Qn, preset, en, reset

  // Notes on the sheet:
  //   中断信号采样参考电路
  //   Reset 
endmodule

module \单周期_多级中断  (
  input  IR1,
  input  IR2,
  input  IR3,
  output RegWrite,
  output MemWrite,
  output [31:0] PC,
  output [31:0] IR,
  output [31:0] RDin,
  output [31:0] MDin,
  output [31:0] LedData
);

  wire CLK, comparator_1_eq, comparator_2_eq, comparator_3_eq, comparator_4_eq, comparator_5_eq, Go, IR1_t,
       IR2_t, IR3_t, IRA, IRB, IRC, or_1_out, or_2_out, W1, W2, W3;
  wire [15:0] \总周期数 ;

  Clock #(.highDuration(1), .lowDuration(1)) clock_1 (.out(CLK));
  Button _1 ();  // open: out
  Button _2 ();  // open: out
  Button _3 ();  // open: out
  Button \u_继续运行  (.out(Go));
  LED #(.active("true")) led_1 (.in(W1));
  LED #(.active("true")) led_2 (.in(W2));
  LED #(.active("true")) led_3 (.in(W3));
  Hex_Digit_Display hex_digit_display_1 (.value(LedData[31:28]));  // open: dp
  Comparator #(.width(16), .mode("twosComplement")) comparator_1 (
    .a(\总周期数 ), .b(16'h7), .eq(comparator_1_eq));  // open: gt, lt
  Comparator #(.width(16), .mode("twosComplement")) comparator_2 (
    .a(\总周期数 ), .b(16'h241), .eq(comparator_2_eq));  // open: gt, lt
  Hex_Digit_Display hex_digit_display_2 (.value(LedData[27:24]));  // open: dp
  Hex_Digit_Display hex_digit_display_3 (.value(LedData[23:20]));  // open: dp
  Comparator #(.width(16), .mode("twosComplement")) comparator_3 (
    .a(16'h258), .b(\总周期数 ), .eq(comparator_3_eq));  // open: gt, lt
  or or_1 (or_1_out, comparator_3_eq, comparator_4_eq);
  Comparator #(.width(16), .mode("twosComplement")) comparator_4 (
    .a(\总周期数 ), .b(16'h1), .eq(comparator_4_eq));  // open: gt, lt
  Comparator #(.width(16), .mode("twosComplement")) comparator_5 (
    .a(\总周期数 ), .b(16'h4), .eq(comparator_5_eq));  // open: gt, lt
  or or_2 (or_2_out, comparator_1_eq, comparator_2_eq);
  Hex_Digit_Display hex_digit_display_4 (.value(LedData[15:12]));  // open: dp
  Hex_Digit_Display hex_digit_display_5 (.value(LedData[19:16]));  // open: dp
  Pull_Resistor #(.pull(0)) pull_resistor_1 (.node(IRA));
  assign IRA = or_1_out ? ~CLK : 1'bz;  // Controlled_Inverter controlled_inverter_1
  Pull_Resistor #(.pull(0)) pull_resistor_2 (.node(IRB));
  assign IRB = comparator_5_eq ? ~CLK : 1'bz;  // Controlled_Inverter controlled_inverter_2
  Pull_Resistor #(.pull(0)) pull_resistor_3 (.node(IRC));
  assign IRC = or_2_out ? ~CLK : 1'bz;  // Controlled_Inverter controlled_inverter_3
  Hex_Digit_Display hex_digit_display_6 (.value(LedData[7:4]));  // open: dp
  Hex_Digit_Display hex_digit_display_7 (.value(LedData[11:8]));  // open: dp
  // Probe on \总周期数 
  Hex_Digit_Display hex_digit_display_8 (.value(LedData[3:0]));  // open: dp
  or or_3 (IR1_t, IR1, IRA);
  or or_4 (IR2_t, IR2, IRB);
  or or_5 (IR3_t, IR3, IRC);

  // Notes on the sheet:
  //   中断源
  //   中断等待指示
  //   总复位信号应将除ROM以外所有存储组件全部清零
  //   多级中断测试信号模拟器
  //   数码管输出
  //   数码管输出应该用寄存器锁存，否则显示数据只能一闪而过
  //   为方便自动评测，需要输出PC，IR，寄存器堆写如数据RDin
  //   RAM写使能MemWrite、RAM写入数据MDin等信号
endmodule

module \封装正确性测试  (
);

  wire IR1, IR2, IR3, MemW, RegW;
  wire [31:0] EX_PC, ID_PC, IF_PC, IR, LED, MDin, MDinr, MEM_PC, PC, RDin, RDinr, WB_PC;

  \单周期RISC_V  \u_单周期risc_v_1  (
    .IR1(IR1), .IR2(IR2), .IR3(IR3), .RegWrite(RegW), .MemWrite(MemW), .PC(PC), .IR(IR), .RDin(RDin),
    .MDin(MDin), .LedData(LED));
  \气泡流水线  \u_气泡流水线_1  (
    .RegWrite(RegW), .MemWrite(MemW), .IF_PC(IF_PC), .ID_PC(ID_PC), .EX_PC(EX_PC), .M_PC(MEM_PC),
    .WB_PC(WB_PC), .RDin(RDinr), .MDin(MDinr), .LedData(LED));
  \单周期_单级中断  \u_单周期_单级中断_1  (
    .IR1(IR1), .IR2(IR2), .IR3(IR3), .RegWrite(RegW), .MemWrite(MemW), .PC(PC), .IR(IR), .RDin(RDin),
    .MDin(MDin), .LedData(LED));
  \理想流水线  \u_理想流水线_1  (
    .RegWrite(RegW), .MemWrite(MemW), .IF_PC(IF_PC), .ID_PC(ID_PC), .EX_PC(EX_PC), .M_PC(MEM_PC),
    .WB_PC(WB_PC), .RDin(RDinr), .MDin(MDinr), .LedData(LED));
  \重定向流水线  \u_重定向流水线_1  (
    .RegWrite(RegW), .MemWrite(MemW), .IF_PC(IF_PC), .ID_PC(ID_PC), .EX_PC(EX_PC), .M_PC(MEM_PC),
    .WB_PC(WB_PC), .RDin(RDinr), .MDin(MDinr), .LedData(LED));
  \单周期_多级中断  \u_单周期_多级中断_1  (
    .IR1(IR1), .IR2(IR2), .IR3(IR3), .RegWrite(RegW), .MemWrite(MemW), .PC(PC), .IR(IR), .RDin(RDin),
    .MDin(MDin), .LedData(LED));

  // Notes on the sheet:
  //   单周期封装测试
  //   气泡流水封装测试
  //   单周期+单级中断封装测试
  //   请检查上面封装有无位宽不匹配，引脚标签是否和连接的标签相对应，否则无法在educoder平台上正确测试
  //   理想流水封装测试
  //   重定向流水封装测试
  //   单周期+多级中断封装测试
endmodule

module IF_ID (
  input  [31:0] \指令字 ,
  input  [31:0] PC,
  input  RST,
  input  Run,
  input  CLK,
  output [31:0] \指令字_2 ,
  output [31:0] PC_2
);

  wire [31:0] multiplexer_1_out, multiplexer_2_out;

  Multiplexer #(.select(1), .width(32), .disabled("Z"), .enable("false")) multiplexer_1 (
    .in0(\指令字 ), .in1({32{1'b0}}), .out(multiplexer_1_out), .sel(RST));
  Multiplexer #(.select(1), .width(32), .disabled("Z"), .enable("false")) multiplexer_2 (
    .in0(PC), .in1({32{1'b0}}), .out(multiplexer_2_out), .sel(RST));
  Register #(.width(32), .trigger("rising"), .Select("low")) register_1 (
    .D(multiplexer_1_out), .en(Run), .Q(\指令字_2 ), .clk(CLK));  // open: clr
  Register #(.width(32), .trigger("rising"), .Select("low")) register_2 (
    .D(multiplexer_2_out), .en(Run), .Q(PC_2), .clk(CLK));  // open: clr
endmodule

module ID_EX (
  input  [4:0] OP,
  input  [4:0] Funct,
  input  Beq,
  input  Bne,
  input  MemToReg,
  input  MemWrite,
  input  [3:0] ALU_OP,
  input  ALU_SRC,
  input  RegWrite,
  input  S_type,
  input  ecall,
  input  Jal,
  input  jalr,
  input  Bltu,
  input  Byte,
  input  [31:0] R1,
  input  [31:0] R2,
  input  [1:0] R1Forward,
  input  [1:0] R2Forward,
  input  [31:0] SignImm,
  input  [4:0] W_num,
  input  [31:0] B_Imm12,
  input  [31:0] U_Imm20,
  input  [31:0] IR,
  input  halt,
  input  [31:0] PC,
  input  RST,
  input  Run,
  input  Clk,
  output [4:0] OP_2,
  output [4:0] Funct_2,
  output Beq_2,
  output bne_2,
  output MemToReg_2,
  output MemWrite_2,
  output [3:0] ALU_OP_2,
  output ALU_SRC_2,
  output RegWrite_2,
  output S_type_2,
  output ecall_2,
  output Jal_2,
  output Jalr_2,
  output Bltu_2,
  output Byte_2,
  output [31:0] R1_2,
  output [31:0] R2_2,
  output [1:0] R1Forward_2,
  output [1:0] R2Forward_2,
  output [31:0] SignImm_2,
  output [4:0] W_num_2,
  output [31:0] B_Imm12_2,
  output [31:0] U_Imm20_2,
  output [31:0] IR_2,
  output halt_2,
  output [31:0] PC_2
);

  wire multiplexer_3_out, multiplexer_4_out, multiplexer_5_out, multiplexer_6_out, multiplexer_8_out,
       multiplexer_9_out, multiplexer_10_out, multiplexer_11_out, multiplexer_12_out, multiplexer_13_out,
       multiplexer_14_out, multiplexer_15_out, multiplexer_25_out;
  wire [1:0] multiplexer_18_out, multiplexer_19_out;
  wire [3:0] multiplexer_7_out;
  wire [4:0] multiplexer_1_out, multiplexer_2_out, multiplexer_21_out;
  wire [31:0] multiplexer_16_out, multiplexer_17_out, multiplexer_20_out, multiplexer_22_out,
       multiplexer_23_out, multiplexer_24_out, multiplexer_26_out;

  Multiplexer #(.select(1), .width(5), .disabled("Z"), .enable("false")) multiplexer_1 (
    .in0(OP), .in1({5{1'b0}}), .out(multiplexer_1_out), .sel(RST));
  Multiplexer #(.select(1), .width(5), .disabled("Z"), .enable("false")) multiplexer_2 (
    .in0(Funct), .in1({5{1'b0}}), .out(multiplexer_2_out), .sel(RST));
  Multiplexer #(.select(1), .width(1), .disabled("Z"), .enable("false")) multiplexer_3 (
    .in0(Beq), .in1(1'b0), .out(multiplexer_3_out), .sel(RST));
  Multiplexer #(.select(1), .width(1), .disabled("Z"), .enable("false")) multiplexer_4 (
    .in0(Bne), .in1(1'b0), .out(multiplexer_4_out), .sel(RST));
  Multiplexer #(.select(1), .width(1), .disabled("Z"), .enable("false")) multiplexer_5 (
    .in0(MemToReg), .in1(1'b0), .out(multiplexer_5_out), .sel(RST));
  Multiplexer #(.select(1), .width(1), .disabled("Z"), .enable("false")) multiplexer_6 (
    .in0(MemWrite), .in1(1'b0), .out(multiplexer_6_out), .sel(RST));
  Multiplexer #(.select(1), .width(4), .disabled("Z"), .enable("false")) multiplexer_7 (
    .in0(ALU_OP), .in1(4'b0000), .out(multiplexer_7_out), .sel(RST));
  Multiplexer #(.select(1), .width(1), .disabled("Z"), .enable("false")) multiplexer_8 (
    .in0(ALU_SRC), .in1(1'b0), .out(multiplexer_8_out), .sel(RST));
  Multiplexer #(.select(1), .width(1), .disabled("Z"), .enable("false")) multiplexer_9 (
    .in0(RegWrite), .in1(1'b0), .out(multiplexer_9_out), .sel(RST));
  Multiplexer #(.select(1), .width(1), .disabled("Z"), .enable("false")) multiplexer_10 (
    .in0(S_type), .in1(1'b0), .out(multiplexer_10_out), .sel(RST));
  Multiplexer #(.select(1), .width(1), .disabled("Z"), .enable("false")) multiplexer_11 (
    .in0(ecall), .in1(1'b0), .out(multiplexer_11_out), .sel(RST));
  Multiplexer #(.select(1), .width(1), .disabled("Z"), .enable("false")) multiplexer_12 (
    .in0(Jal), .in1(1'b0), .out(multiplexer_12_out), .sel(RST));
  Multiplexer #(.select(1), .width(1), .disabled("Z"), .enable("false")) multiplexer_13 (
    .in0(jalr), .in1(1'b0), .out(multiplexer_13_out), .sel(RST));
  Multiplexer #(.select(1), .width(1), .disabled("Z"), .enable("false")) multiplexer_14 (
    .in0(Bltu), .in1(1'b0), .out(multiplexer_14_out), .sel(RST));
  Multiplexer #(.select(1), .width(1), .disabled("Z"), .enable("false")) multiplexer_15 (
    .in0(Byte), .in1(1'b0), .out(multiplexer_15_out), .sel(RST));
  Multiplexer #(.select(1), .width(32), .disabled("Z"), .enable("false")) multiplexer_16 (
    .in0(R1), .in1({32{1'b0}}), .out(multiplexer_16_out), .sel(RST));
  Multiplexer #(.select(1), .width(32), .disabled("Z"), .enable("false")) multiplexer_17 (
    .in0(R2), .in1({32{1'b0}}), .out(multiplexer_17_out), .sel(RST));
  Multiplexer #(.select(1), .width(2), .disabled("Z"), .enable("false")) multiplexer_18 (
    .in0(R1Forward), .in1(2'b00), .out(multiplexer_18_out), .sel(RST));
  Multiplexer #(.select(1), .width(2), .disabled("Z"), .enable("false")) multiplexer_19 (
    .in0(R2Forward), .in1(2'b00), .out(multiplexer_19_out), .sel(RST));
  Multiplexer #(.select(1), .width(32), .disabled("Z"), .enable("false")) multiplexer_20 (
    .in0(SignImm), .in1({32{1'b0}}), .out(multiplexer_20_out), .sel(RST));
  Multiplexer #(.select(1), .width(5), .disabled("Z"), .enable("false")) multiplexer_21 (
    .in0(W_num), .in1({5{1'b0}}), .out(multiplexer_21_out), .sel(RST));
  Multiplexer #(.select(1), .width(32), .disabled("Z"), .enable("false")) multiplexer_22 (
    .in0(B_Imm12), .in1({32{1'b0}}), .out(multiplexer_22_out), .sel(RST));
  Multiplexer #(.select(1), .width(32), .disabled("Z"), .enable("false")) multiplexer_23 (
    .in0(U_Imm20), .in1({32{1'b0}}), .out(multiplexer_23_out), .sel(RST));
  Multiplexer #(.select(1), .width(32), .disabled("Z"), .enable("false")) multiplexer_24 (
    .in0(IR), .in1({32{1'b0}}), .out(multiplexer_24_out), .sel(RST));
  Multiplexer #(.select(1), .width(1), .disabled("Z"), .enable("false")) multiplexer_25 (
    .in0(halt), .in1(1'b0), .out(multiplexer_25_out), .sel(RST));
  Multiplexer #(.select(1), .width(32), .disabled("Z"), .enable("false")) multiplexer_26 (
    .in0(PC), .in1({32{1'b0}}), .out(multiplexer_26_out), .sel(RST));
  Register #(.width(5), .trigger("rising"), .Select("low")) register_1 (
    .D(multiplexer_1_out), .en(Run), .Q(OP_2), .clk(Clk));  // open: clr
  Register #(.width(5), .trigger("rising"), .Select("low")) register_2 (
    .D(multiplexer_2_out), .en(Run), .Q(Funct_2), .clk(Clk));  // open: clr
  Register #(.width(1), .trigger("rising"), .Select("low")) register_3 (
    .D(multiplexer_3_out), .en(Run), .Q(Beq_2), .clk(Clk));  // open: clr
  Register #(.width(1), .trigger("rising"), .Select("low")) register_4 (
    .D(multiplexer_4_out), .en(Run), .Q(bne_2), .clk(Clk));  // open: clr
  Register #(.width(1), .trigger("rising"), .Select("low")) register_5 (
    .D(multiplexer_5_out), .en(Run), .Q(MemToReg_2), .clk(Clk));  // open: clr
  Register #(.width(1), .trigger("rising"), .Select("low")) register_6 (
    .D(multiplexer_6_out), .en(Run), .Q(MemWrite_2), .clk(Clk));  // open: clr
  Register #(.width(4), .trigger("rising"), .Select("low")) register_7 (
    .D(multiplexer_7_out), .en(Run), .Q(ALU_OP_2), .clk(Clk));  // open: clr
  Register #(.width(1), .trigger("rising"), .Select("low")) register_8 (
    .D(multiplexer_8_out), .en(Run), .Q(ALU_SRC_2), .clk(Clk));  // open: clr
  Register #(.width(1), .trigger("rising"), .Select("low")) register_9 (
    .D(multiplexer_9_out), .en(Run), .Q(RegWrite_2), .clk(Clk));  // open: clr
  Register #(.width(1), .trigger("rising"), .Select("low")) register_10 (
    .D(multiplexer_10_out), .en(Run), .Q(S_type_2), .clk(Clk));  // open: clr
  Register #(.width(1), .trigger("rising"), .Select("low")) register_11 (
    .D(multiplexer_11_out), .en(Run), .Q(ecall_2), .clk(Clk));  // open: clr
  Register #(.width(1), .trigger("rising"), .Select("low")) register_12 (
    .D(multiplexer_12_out), .en(Run), .Q(Jal_2), .clk(Clk));  // open: clr
  Register #(.width(1), .trigger("rising"), .Select("low")) register_13 (
    .D(multiplexer_13_out), .en(Run), .Q(Jalr_2), .clk(Clk));  // open: clr
  Register #(.width(1), .trigger("rising"), .Select("low")) register_14 (
    .D(multiplexer_14_out), .en(Run), .Q(Bltu_2), .clk(Clk));  // open: clr
  Register #(.width(1), .trigger("rising"), .Select("low")) register_15 (
    .D(multiplexer_15_out), .en(Run), .Q(Byte_2), .clk(Clk));  // open: clr
  Register #(.width(32), .trigger("rising"), .Select("low")) register_16 (
    .D(multiplexer_16_out), .en(Run), .Q(R1_2), .clk(Clk));  // open: clr
  Register #(.width(32), .trigger("rising"), .Select("low")) register_17 (
    .D(multiplexer_17_out), .en(Run), .Q(R2_2), .clk(Clk));  // open: clr
  Register #(.width(2), .trigger("rising"), .Select("low")) register_18 (
    .D(multiplexer_18_out), .en(Run), .Q(R1Forward_2), .clk(Clk));  // open: clr
  Register #(.width(2), .trigger("rising"), .Select("low")) register_19 (
    .D(multiplexer_19_out), .en(Run), .Q(R2Forward_2), .clk(Clk));  // open: clr
  Register #(.width(32), .trigger("rising"), .Select("low")) register_20 (
    .D(multiplexer_20_out), .en(Run), .Q(SignImm_2), .clk(Clk));  // open: clr
  Register #(.width(5), .trigger("rising"), .Select("low")) register_21 (
    .D(multiplexer_21_out), .en(Run), .Q(W_num_2), .clk(Clk));  // open: clr
  Register #(.width(32), .trigger("rising"), .Select("low")) register_22 (
    .D(multiplexer_22_out), .en(Run), .Q(B_Imm12_2), .clk(Clk));  // open: clr
  Register #(.width(32), .trigger("rising"), .Select("low")) register_23 (
    .D(multiplexer_23_out), .en(Run), .Q(U_Imm20_2), .clk(Clk));  // open: clr
  Register #(.width(32), .trigger("rising"), .Select("low")) register_24 (
    .D(multiplexer_24_out), .en(Run), .Q(IR_2), .clk(Clk));  // open: clr
  Register #(.width(1), .trigger("rising"), .Select("low")) register_25 (
    .D(multiplexer_25_out), .en(Run), .Q(halt_2), .clk(Clk));  // open: clr
  Register #(.width(32), .trigger("rising"), .Select("low")) register_26 (
    .D(multiplexer_26_out), .en(Run), .Q(PC_2), .clk(Clk));  // open: clr
endmodule

module EX_MEM (
  input  [4:0] OP,
  input  [4:0] Funct,
  input  Beq,
  input  Bne,
  input  MemToReg,
  input  MemWrite,
  input  [3:0] ALU_OP,
  input  ALU_SRC,
  input  RegWrite,
  input  S_type,
  input  equal,
  input  Jal,
  input  jalr,
  input  Bltu,
  input  Byte,
  input  [31:0] Result,
  input  [31:0] WriteData,
  input  [4:0] W_num,
  input  [31:0] B_Imm12,
  input  [31:0] U_Imm20,
  input  [31:0] IR,
  input  halt,
  input  [31:0] PC,
  input  RST,
  input  Run,
  input  Clk,
  output [4:0] OP_2,
  output [4:0] Funct_2,
  output Beq_2,
  output bne_2,
  output MemToReg_2,
  output MemWrite_2,
  output [3:0] ALU_OP_2,
  output ALU_SRC_2,
  output RegWrite_2,
  output S_type_2,
  output equal_2,
  output Jal_2,
  output Jalr_2,
  output Bltu_2,
  output Byte_2,
  output [31:0] Result_2,
  output [31:0] WriteData_2,
  output [4:0] W_num_2,
  output [31:0] B_Imm12_2,
  output [31:0] U_Imm20_2,
  output [31:0] IR_2,
  output halt_2,
  output [31:0] PC_2
);

  Register #(.width(5), .trigger("rising"), .Select("low")) register_1 (
    .D(OP), .en(Run), .Q(OP_2), .clk(Clk), .clr(RST));
  Register #(.width(5), .trigger("rising"), .Select("low")) register_2 (
    .D(Funct), .en(Run), .Q(Funct_2), .clk(Clk), .clr(RST));
  Register #(.width(1), .trigger("rising"), .Select("low")) register_3 (
    .D(Beq), .en(Run), .Q(Beq_2), .clk(Clk), .clr(RST));
  Register #(.width(1), .trigger("rising"), .Select("low")) register_4 (
    .D(Bne), .en(Run), .Q(bne_2), .clk(Clk), .clr(RST));
  Register #(.width(1), .trigger("rising"), .Select("low")) register_5 (
    .D(MemToReg), .en(Run), .Q(MemToReg_2), .clk(Clk), .clr(RST));
  Register #(.width(1), .trigger("rising"), .Select("low")) register_6 (
    .D(MemWrite), .en(Run), .Q(MemWrite_2), .clk(Clk), .clr(RST));
  Register #(.width(4), .trigger("rising"), .Select("low")) register_7 (
    .D(ALU_OP), .en(Run), .Q(ALU_OP_2), .clk(Clk), .clr(RST));
  Register #(.width(1), .trigger("rising"), .Select("low")) register_8 (
    .D(ALU_SRC), .en(Run), .Q(ALU_SRC_2), .clk(Clk), .clr(RST));
  Register #(.width(1), .trigger("rising"), .Select("low")) register_9 (
    .D(RegWrite), .en(Run), .Q(RegWrite_2), .clk(Clk), .clr(RST));
  Register #(.width(1), .trigger("rising"), .Select("low")) register_10 (
    .D(S_type), .en(Run), .Q(S_type_2), .clk(Clk), .clr(RST));
  Register #(.width(1), .trigger("rising"), .Select("low")) register_11 (
    .D(equal), .en(Run), .Q(equal_2), .clk(Clk), .clr(RST));
  Register #(.width(1), .trigger("rising"), .Select("low")) register_12 (
    .D(Jal), .en(Run), .Q(Jal_2), .clk(Clk), .clr(RST));
  Register #(.width(1), .trigger("rising"), .Select("low")) register_13 (
    .D(jalr), .en(Run), .Q(Jalr_2), .clk(Clk), .clr(RST));
  Register #(.width(1), .trigger("rising"), .Select("low")) register_14 (
    .D(Bltu), .en(Run), .Q(Bltu_2), .clk(Clk), .clr(RST));
  Register #(.width(1), .trigger("rising"), .Select("low")) register_15 (
    .D(Byte), .en(Run), .Q(Byte_2), .clk(Clk), .clr(RST));
  Register #(.width(32), .trigger("rising"), .Select("low")) register_16 (
    .D(Result), .en(Run), .Q(Result_2), .clk(Clk), .clr(RST));
  Register #(.width(32), .trigger("rising"), .Select("low")) register_17 (
    .D(WriteData), .en(Run), .Q(WriteData_2), .clk(Clk), .clr(RST));
  Register #(.width(5), .trigger("rising"), .Select("low")) register_18 (
    .D(W_num), .en(Run), .Q(W_num_2), .clk(Clk), .clr(RST));
  Register #(.width(32), .trigger("rising"), .Select("low")) register_19 (
    .D(B_Imm12), .en(Run), .Q(B_Imm12_2), .clk(Clk), .clr(RST));
  Register #(.width(32), .trigger("rising"), .Select("low")) register_20 (
    .D(U_Imm20), .en(Run), .Q(U_Imm20_2), .clk(Clk), .clr(RST));
  Register #(.width(32), .trigger("rising"), .Select("low")) register_21 (
    .D(IR), .en(Run), .Q(IR_2), .clk(Clk), .clr(RST));
  Register #(.width(1), .trigger("rising"), .Select("low")) register_22 (
    .D(halt), .en(Run), .Q(halt_2), .clk(Clk), .clr(RST));
  Register #(.width(32), .trigger("rising"), .Select("low")) register_23 (
    .D(PC), .en(Run), .Q(PC_2), .clk(Clk), .clr(RST));
endmodule

module MEM_WB (
  input  MemToReg,
  input  RegWrite,
  input  Jal,
  input  jalr,
  input  Bltu,
  input  Byte,
  input  [31:0] AluResult,
  input  [31:0] RD,
  input  [4:0] W_num,
  input  [31:0] IR,
  input  halt,
  input  [31:0] PC,
  input  RST,
  input  Run,
  input  Clk,
  output MemToReg_2,
  output RegWrite_2,
  output Jal_2,
  output Jalr_2,
  output Bltu_2,
  output Byte_2,
  output [31:0] AluResult_2,
  output [31:0] RD_2,
  output [4:0] W_num_2,
  output [31:0] IR_2,
  output halt_2,
  output [31:0] PC_2
);

  Register #(.width(1), .trigger("rising"), .Select("low")) register_1 (
    .D(MemToReg), .en(Run), .Q(MemToReg_2), .clk(Clk), .clr(RST));
  Register #(.width(1), .trigger("rising"), .Select("low")) register_2 (
    .D(RegWrite), .en(Run), .Q(RegWrite_2), .clk(Clk), .clr(RST));
  Register #(.width(1), .trigger("rising"), .Select("low")) register_3 (
    .D(Jal), .en(Run), .Q(Jal_2), .clk(Clk), .clr(RST));
  Register #(.width(1), .trigger("rising"), .Select("low")) register_4 (
    .D(jalr), .en(Run), .Q(Jalr_2), .clk(Clk), .clr(RST));
  Register #(.width(1), .trigger("rising"), .Select("low")) register_5 (
    .D(Bltu), .en(Run), .Q(Bltu_2), .clk(Clk), .clr(RST));
  Register #(.width(1), .trigger("rising"), .Select("low")) register_6 (
    .D(Byte), .en(Run), .Q(Byte_2), .clk(Clk), .clr(RST));
  Register #(.width(32), .trigger("rising"), .Select("low")) register_7 (
    .D(AluResult), .en(Run), .Q(AluResult_2), .clk(Clk), .clr(RST));
  Register #(.width(32), .trigger("rising"), .Select("low")) register_8 (
    .D(RD), .en(Run), .Q(RD_2), .clk(Clk), .clr(RST));
  Register #(.width(5), .trigger("rising"), .Select("low")) register_9 (
    .D(W_num), .en(Run), .Q(W_num_2), .clk(Clk), .clr(RST));
  Register #(.width(32), .trigger("rising"), .Select("low")) register_10 (
    .D(IR), .en(Run), .Q(IR_2), .clk(Clk), .clr(RST));
  Register #(.width(1), .trigger("rising"), .Select("low")) register_11 (
    .D(halt), .en(Run), .Q(halt_2), .clk(Clk), .clr(RST));
  Register #(.width(32), .trigger("rising"), .Select("low")) register_12 (
    .D(PC), .en(Run), .Q(PC_2), .clk(Clk), .clr(RST));
endmodule
